// Logisim project HIB_CPU.circ as structural Verilog: 80 circuits, main circuit main
module main (
);

  wire bcd_to_display_32bit_1_de, BE, BSS, button_1_out, CLK, CLR, CWE, DSS, DWE, Equal, Greater, LE, Less,
       NC, or_1_out, or_2_out, or_3_out, Pause, xnor_1_out;
  wire [2:0] alu_32bit_1_less, Cond, CRA;
  wire [3:0] AFS;
  wire [6:0] bcd_to_display_32bit_1_dout, multiplexer_8_out;
  wire [17:8] OP;
  wire [19:0] multiplexer_2_out;
  wire [31:0] alu_32bit_1_alu_out, alu_32bit_1_alu_upper_out, Disp, multiplexer_1_out, multiplexer_3_out,
       multiplexer_5_out, multiplexer_7_out, program_counter_1_count, register_file_2x2_32_1_dout_a,
       register_file_2x2_32_1_dout_b, Zero_dout;
  wire [31:16] rom_1_data;

  Clock clock_1 (.out(CLK));
  Program_counter program_counter_1 (
    .Load(LE), .Enable(xnor_1_out), .Clk(CLK), .Reset(button_1_out), .Data(multiplexer_1_out),
    .Count(program_counter_1_count));
  Button button_1 (.out(button_1_out));
  // Probe on program_counter_1_count[23:0]
  xnor xnor_1 (xnor_1_out, BE, Pause);
  ROM #(.addrWidth(24), .dataWidth(32)) rom_1 (
    .addr(program_counter_1_count[23:0]),
    .data({rom_1_data[31:23], CRA, rom_1_data[19:16], multiplexer_2_out[15:0]}));
  ROM #(.dataWidth(19)) rom_2 (
    .addr(rom_1_data[31:24]), .data({BE, OP[17], CWE, AFS, OP[11:8], DSS, BSS, Cond, NC, CLR, DWE}));
  Multiplexer #(.width(32)) multiplexer_1 (
    .in0({{12{1'b0}}, multiplexer_2_out}), .in1(register_file_2x2_32_1_dout_a), .out(multiplexer_1_out),
    .sel(BSS));
  Multiplexer #(.width(4)) multiplexer_2 (
    .in0(4'b0000), .in1(rom_1_data[19:16]), .out(multiplexer_2_out[19:16]), .sel(LE));
  Register_32bit Zero (.Dout(Zero_dout));  // open: Din, Write, Clk, Reset
  Multiplexer #(.select(2), .width(32)) multiplexer_3 (
    .in0({{12{1'b0}}, multiplexer_2_out}), .in1(alu_32bit_1_alu_out), .in2(register_file_2x2_32_1_dout_a),
    .in3(Zero_dout), .out(multiplexer_3_out), .sel(OP[11:10]));
  Multiplexer #(.select(3)) multiplexer_4 (
    .in0(NC), .in1(Less), .in2(Greater), .in3(Equal), .in4(or_1_out), .in5(or_2_out), .out(LE), .sel(Cond));  // open: in6, in7
  // Probe on Cond
  Multiplexer #(.width(32)) multiplexer_5 (
    .in0({{12{1'b0}}, multiplexer_2_out}),
    .in1({multiplexer_2_out[15:0], {12{1'b0}}, multiplexer_2_out[19:16]}), .out(multiplexer_5_out),
    .sel(OP[17]));
  register_file_2x2_32 register_file_2x2_32_1 (
    .WE_A(OP[8]), .WE_B(OP[9]), .WAddr_A({rom_1_data[23], CRA}), .WAddr_B(multiplexer_2_out[15:12]),
    .Din_A(multiplexer_3_out), .Din_B(alu_32bit_1_alu_upper_out), .RAddr_A(rom_1_data[19:16]),
    .RAddr_B(multiplexer_2_out[3:0]), .Clk(CLK), .Dout_B(register_file_2x2_32_1_dout_b),
    .Dout_A(register_file_2x2_32_1_dout_a));
  Multiplexer #(.width(32)) multiplexer_6 (
    .in0(multiplexer_5_out), .in1(register_file_2x2_32_1_dout_a), .out(Disp), .sel(DSS));
  Multiplexer #(.width(32)) multiplexer_7 (
    .in0(multiplexer_5_out), .in1(register_file_2x2_32_1_dout_b), .out(multiplexer_7_out), .sel(DSS));
  or or_1 (or_1_out, Less, Equal);
  or or_2 (or_2_out, Greater, Equal);
  // Probe on Disp
  ALU_32bit alu_32bit_1 (
    .A(register_file_2x2_32_1_dout_a), .B(multiplexer_7_out), .S(AFS), .ALU_out(alu_32bit_1_alu_out),
    .ALU_Upper_out(alu_32bit_1_alu_upper_out), .Less(alu_32bit_1_less[0]), .Equal(alu_32bit_1_less[1]),
    .Greater(alu_32bit_1_less[2]));  // open: Cin, Cout, Zero
  // Probe on CRA
  // Probe on multiplexer_8_out
  BCD_TO_DISPLAY_32bit bcd_to_display_32bit_1 (
    .Din(Disp), .Enable(BE), .CLK(CLK), .Dout(bcd_to_display_32bit_1_dout), .DE(bcd_to_display_32bit_1_de),
    .Reset(Pause));
  // Probe on alu_32bit_1_less
  // Probe on CRA
  Multiplexer #(.width(7)) multiplexer_8 (
    .in0(Disp[6:0]), .in1(bcd_to_display_32bit_1_dout), .out(multiplexer_8_out),
    .sel(bcd_to_display_32bit_1_de));
  TTY tty_1 (.data(multiplexer_8_out), .clk(CLK), .we(or_3_out), .clr(CLR));
  or or_3 (or_3_out, bcd_to_display_32bit_1_de, DWE);
  register_file_3bit register_file_3bit_1 (
    .WE(CWE), .WAddr(CRA), .Data_in(alu_32bit_1_less), .Clk(CLK), .RAddr(CRA),
    .Data_out({Greater, Equal, Less}));

  // Other names for the same wires on the sheet: OP (some bits) = {BE, CWE, AFS, DSS, BSS, Cond, NC, CLR, DWE};
  //   WE[1:0] = OP[9:8]; RSS[1:0] = OP[11:10]; Up = OP[17]

  // Notes on the sheet:
  //   contents of rom_1 (hex, n*v repeats v):
  //   25000000 200ffff 300ffff 5000069 500006e 5000074 5000020 500006d 5000061 5000078 500003a 5000020
  //   26000000 500000a 5000035 5000078 5000035 500003d 24100000 24200000 d110005 d220001 20020005 16000014
  //   26010000 500000a 2100005 10110001 5000035 5000078 5000035 500003d 26010000 500000a 5000035 500002b
  //   5000035 500003d 2800005 d880005 26080000 500000a 2900064 2a0003f 27000064 500002d 2700003f 500003d
  //   eb9000a 260b0000 500000a 24300000 2300100 27000100 500002a 27000004 500003d 23330002 26030000
  //   500000a 2e0ffff 260e0000 5000020 5000049 500006e 5000076 5000065 5000072 5000074 5000065 5000064
  //   500003a 5000020 21de0000 260d0000 500000a 5000045 5000078 5000070 5000065 5000063 5000074 5000065
  //   5000064 500003a 5000020 24e00000 3eeffff 260e0000 1400005b 2001234 1400005b
  //   contents of rom_2 (hex, n*v repeats v):
  //   0 980 100 21500 81 1 580 500 2580 2500 1580 1500 3580 3500 7580 7500 8580 8700 8780 44 4 48 8 50 10
  //   58 18 60 20 68 28 10080 10000 5500 4500 6500 d00 2 40080 40000
  //   DWE: Display Write Enable - 1
  //   CLR: Clear Display - 1
  //   NC: No Conditional - 1
  //   Cond: Which Conditional - 3
  //   BSS: Branch Source Select - 1
  //   DSS: Data Source Select - 1
  //   WE: Write Enable - 2
  //   RSS: Register Source Select - 2
  //   AFS: ALU Func select - 4
  //   CWE: Conditional Write Enable - 1
  //   Up: Move data to top 16 bits - 1
  //   BE: BCD Enable - 1
endmodule

module MUX2to1_1bit (
  input  A,
  input  B,
  input  S,
  output F
);

  wire and_1_out, and_2_out, not_1_out;

  and and_1 (and_1_out, A, not_1_out);
  not not_1 (not_1_out, S);
  and and_2 (and_2_out, B, S);
  or or_1 (F, and_1_out, and_2_out);
endmodule

module MUX2to1_4bit (
  input  [3:0] A,
  input  [3:0] B,
  input  S,
  output [3:0] F
);

  MUX2to1_1bit mux2to1_1bit_1 (.A(A[3]), .B(B[3]), .S(S), .F(F[3]));
  MUX2to1_1bit mux2to1_1bit_2 (.A(A[2]), .B(B[2]), .S(S), .F(F[2]));
  MUX2to1_1bit mux2to1_1bit_3 (.A(A[1]), .B(B[1]), .S(S), .F(F[1]));
  MUX2to1_1bit mux2to1_1bit_4 (.A(A[0]), .B(B[0]), .S(S), .F(F[0]));
endmodule

module Full_Adder (
  input  A,
  input  B,
  input  Cin,
  output S,
  output Cout
);

  wire and_1_out, and_2_out, and_3_out;

  xor xor_1 (S, A, B, Cin);
  and and_1 (and_1_out, A, B);
  and and_2 (and_2_out, B, Cin);
  and and_3 (and_3_out, A, Cin);
  or or_1 (Cout, and_1_out, and_2_out, and_3_out);
endmodule

module AND_4bit (
  input  [3:0] A,
  input  [3:0] B,
  output [3:0] AND4
);

  and and_1 (AND4[3], A[3], B[3]);
  and and_2 (AND4[2], A[2], B[2]);
  and and_3 (AND4[1], A[1], B[1]);
  and and_4 (AND4[0], A[0], B[0]);
endmodule

module OR_4bit (
  input  [3:0] A,
  input  [3:0] B,
  output [3:0] OR4
);

  or or_1 (OR4[3], A[3], B[3]);
  or or_2 (OR4[2], A[2], B[2]);
  or or_3 (OR4[1], A[1], B[1]);
  or or_4 (OR4[0], A[0], B[0]);
endmodule

module XOR_4bit (
  input  [3:0] A,
  input  [3:0] B,
  output [3:0] XOR4
);

  xor xor_1 (XOR4[3], A[3], B[3]);
  xor xor_2 (XOR4[2], A[2], B[2]);
  xor xor_3 (XOR4[1], A[1], B[1]);
  xor xor_4 (XOR4[0], A[0], B[0]);
endmodule

module MUX4to1_4bit (
  input  [3:0] IN0,
  input  [3:0] IN2,
  input  [3:0] IN1,
  input  [3:0] IN3,
  input  [1:0] S,
  output [3:0] MUX_out
);

  wire [3:0] mux2to1_4bit_1_f, mux2to1_4bit_2_f;

  MUX2to1_4bit mux2to1_4bit_1 (.A(IN0), .B(IN2), .S(S[1]), .F(mux2to1_4bit_1_f));
  MUX2to1_4bit mux2to1_4bit_2 (.A(IN1), .B(IN3), .S(S[1]), .F(mux2to1_4bit_2_f));
  MUX2to1_4bit mux2to1_4bit_3 (.A(mux2to1_4bit_1_f), .B(mux2to1_4bit_2_f), .S(S[0]), .F(MUX_out));

  // Notes on the sheet:
  //   (A input)
  //   (C input)
  //   (B input)
  //   (D input)
  //   Joshua Cox
  //   (F)
endmodule

module Add_4bit (
  input  [3:0] A,
  input  [3:0] B,
  input  Cin,
  output [3:0] ADD4,
  output Cout
);

  wire full_adder_1_cout, full_adder_2_cout, full_adder_3_cout;

  Full_Adder full_adder_1 (.A(A[0]), .B(B[0]), .Cin(Cin), .S(ADD4[0]), .Cout(full_adder_1_cout));
  Full_Adder full_adder_2 (.A(A[1]), .B(B[1]), .Cin(full_adder_1_cout), .S(ADD4[1]), .Cout(full_adder_2_cout));
  Full_Adder full_adder_3 (.A(A[2]), .B(B[2]), .Cin(full_adder_2_cout), .S(ADD4[2]), .Cout(full_adder_3_cout));
  Full_Adder full_adder_4 (.A(A[3]), .B(B[3]), .Cin(full_adder_3_cout), .S(ADD4[3]), .Cout(Cout));

  // Notes on the sheet:
  //   Joshua Cox
endmodule

module LSR_4bit (
  input  [3:0] A,
  output [3:0] LSR4,
  output Lost
);


  assign Lost = A[3];
  assign LSR4 = {A[2:0], 1'b0};
endmodule

module LSL_4bit (
  input  [3:0] A,
  output [3:0] LSL4,
  output Lost
);


  assign Lost = A[0];
  assign LSL4 = {1'b0, A[3:1]};
endmodule

module Invert_4bit (
  input  [3:0] A,
  output [3:0] Invert4
);

  not not_1 (Invert4[0], A[0]);
  not not_2 (Invert4[1], A[1]);
  not not_3 (Invert4[2], A[2]);
  not not_4 (Invert4[3], A[3]);
endmodule

module MUX8to1_4bit (
  input  [3:0] IN0,
  input  [3:0] IN2,
  input  [3:0] IN1,
  input  [3:0] IN3,
  input  [3:0] IN4,
  input  [3:0] IN6,
  input  [3:0] IN5,
  input  [3:0] IN7,
  input  [2:0] S,
  output [3:0] F
);

  wire [3:0] mux4to1_4bit_1_mux_out, mux4to1_4bit_2_mux_out;

  MUX4to1_4bit mux4to1_4bit_1 (
    .IN0(IN0), .IN2(IN2), .IN1(IN1), .IN3(IN3), .S(S[1:0]), .MUX_out(mux4to1_4bit_1_mux_out));
  MUX4to1_4bit mux4to1_4bit_2 (
    .IN0(IN4), .IN2(IN6), .IN1(IN5), .IN3(IN7), .S(S[1:0]), .MUX_out(mux4to1_4bit_2_mux_out));
  MUX2to1_4bit mux2to1_4bit_1 (.A(mux4to1_4bit_1_mux_out), .B(mux4to1_4bit_2_mux_out), .S(S[2]), .F(F));
endmodule

module Counter_8bit (
  input  Clock_in,
  output [7:0] Count,
  output Clock_out
);

  wire d_ff_1_q, d_ff_2_q, d_ff_3_q, d_ff_4_q, d_ff_5_q, d_ff_6_q, d_ff_7_q;

  D_Flip_Flop d_ff_1 (.D(Count[0]), .clk(Clock_in), .Q(d_ff_1_q), .Qn(Count[0]));  // open: preset, reset
  D_Flip_Flop d_ff_2 (.D(Count[1]), .clk(d_ff_1_q), .Q(d_ff_2_q), .Qn(Count[1]));  // open: preset, reset
  D_Flip_Flop d_ff_3 (.D(Count[2]), .clk(d_ff_2_q), .Q(d_ff_3_q), .Qn(Count[2]));  // open: preset, reset
  D_Flip_Flop d_ff_4 (.D(Count[3]), .clk(d_ff_3_q), .Q(d_ff_4_q), .Qn(Count[3]));  // open: preset, reset
  D_Flip_Flop d_ff_5 (.D(Count[4]), .clk(d_ff_4_q), .Q(d_ff_5_q), .Qn(Count[4]));  // open: preset, reset
  D_Flip_Flop d_ff_6 (.D(Count[5]), .clk(d_ff_5_q), .Q(d_ff_6_q), .Qn(Count[5]));  // open: preset, reset
  D_Flip_Flop d_ff_7 (.D(Count[6]), .clk(d_ff_6_q), .Q(d_ff_7_q), .Qn(Count[6]));  // open: preset, reset
  D_Flip_Flop d_ff_8 (.D(Count[7]), .clk(d_ff_7_q), .Q(Clock_out), .Qn(Count[7]));  // open: preset, reset
endmodule

module Counter_64bit (
  input  Clock_in,
  output [63:0] Count,
  output Clock_out
);

  wire counter_8bit_1_clock_out, counter_8bit_2_clock_out, counter_8bit_3_clock_out,
       counter_8bit_4_clock_out, counter_8bit_5_clock_out, counter_8bit_6_clock_out, counter_8bit_7_clock_out;

  Counter_8bit counter_8bit_1 (.Clock_in(Clock_in), .Count(Count[7:0]), .Clock_out(counter_8bit_1_clock_out));
  Counter_8bit counter_8bit_2 (
    .Clock_in(counter_8bit_7_clock_out), .Count(Count[39:32]), .Clock_out(counter_8bit_2_clock_out));
  Counter_8bit counter_8bit_3 (
    .Clock_in(counter_8bit_1_clock_out), .Count(Count[15:8]), .Clock_out(counter_8bit_3_clock_out));
  Counter_8bit counter_8bit_4 (
    .Clock_in(counter_8bit_2_clock_out), .Count(Count[47:40]), .Clock_out(counter_8bit_4_clock_out));
  Counter_8bit counter_8bit_5 (
    .Clock_in(counter_8bit_3_clock_out), .Count(Count[23:16]), .Clock_out(counter_8bit_5_clock_out));
  Counter_8bit counter_8bit_6 (
    .Clock_in(counter_8bit_4_clock_out), .Count(Count[55:48]), .Clock_out(counter_8bit_6_clock_out));
  Counter_8bit counter_8bit_7 (
    .Clock_in(counter_8bit_5_clock_out), .Count(Count[31:24]), .Clock_out(counter_8bit_7_clock_out));
  Counter_8bit counter_8bit_8 (.Clock_in(counter_8bit_6_clock_out), .Count(Count[63:56]), .Clock_out(Clock_out));
endmodule

module AND_8bit (
  input  [7:0] A,
  input  [7:0] B,
  output [7:0] out_3
);

  AND_4bit and_4bit_1 (.A(A[3:0]), .B(B[3:0]), .AND4(out_3[3:0]));
  AND_4bit and_4bit_2 (.A(A[7:4]), .B(B[7:4]), .AND4(out_3[7:4]));
endmodule

module OR_8bit (
  input  [7:0] A,
  input  [7:0] B,
  output [7:0] out_3
);

  OR_4bit or_4bit_1 (.A(A[3:0]), .B(B[3:0]), .OR4(out_3[3:0]));
  OR_4bit or_4bit_2 (.A(A[7:4]), .B(B[7:4]), .OR4(out_3[7:4]));
endmodule

module XOR_8bit (
  input  [7:0] A,
  input  [7:0] B,
  output [7:0] out_3
);

  XOR_4bit xor_4bit_1 (.A(A[3:0]), .B(B[3:0]), .XOR4(out_3[3:0]));
  XOR_4bit xor_4bit_2 (.A(A[7:4]), .B(B[7:4]), .XOR4(out_3[7:4]));
endmodule

module ADD_8bit (
  input  [7:0] A,
  input  [7:0] B,
  input  Cin,
  output [7:0] ADD8,
  output Cout
);

  wire add_4bit_1_cout;

  Add_4bit add_4bit_1 (.A(A[3:0]), .B(B[3:0]), .Cin(Cin), .ADD4(ADD8[3:0]), .Cout(add_4bit_1_cout));
  Add_4bit add_4bit_2 (.A(A[7:4]), .B(B[7:4]), .Cin(add_4bit_1_cout), .ADD4(ADD8[7:4]), .Cout(Cout));
endmodule

module LSR_8bit (
  input  [7:0] A,
  output [7:0] LSR4,
  output Lost
);


  assign Lost = A[0];
  assign LSR4 = {1'b0, A[7:1]};

  // Notes on the sheet:
  //   Joshua Cox
endmodule

module LSL_8bit (
  input  [7:0] in_1,
  output [7:0] out_2,
  output out_3
);


  assign out_2 = {in_1[6:0], 1'b0};
  assign out_3 = in_1[7];

  // Notes on the sheet:
  //   Joshua Cox
endmodule

module Invert_8bit (
  input  [7:0] A,
  output [7:0] Invert4
);

  not not_1 (Invert4[0], A[0]);
  not not_2 (Invert4[1], A[1]);
  not not_3 (Invert4[2], A[2]);
  not not_4 (Invert4[3], A[3]);
  not not_5 (Invert4[4], A[4]);
  not not_6 (Invert4[5], A[5]);
  not not_7 (Invert4[6], A[6]);
  not not_8 (Invert4[7], A[7]);

  // Notes on the sheet:
  //   Joshua Cox
endmodule

module MUX2to1_8bit (
  input  [7:0] A,
  input  [7:0] B,
  input  S,
  output [7:0] F
);

  MUX2to1_4bit mux2to1_4bit_1 (.A(A[3:0]), .B(B[3:0]), .S(S), .F(F[3:0]));
  MUX2to1_4bit mux2to1_4bit_2 (.A(A[7:4]), .B(B[7:4]), .S(S), .F(F[7:4]));
endmodule

module MUX4to1_8bit (
  input  [7:0] IN0,
  input  [7:0] IN2,
  input  [7:0] IN1,
  input  [7:0] IN3,
  input  [1:0] S,
  output [7:0] MUX_out
);

  wire [7:0] mux2to1_8bit_1_f, mux2to1_8bit_2_f;

  MUX2to1_8bit mux2to1_8bit_1 (.A(IN0), .B(IN2), .S(S[1]), .F(mux2to1_8bit_1_f));
  MUX2to1_8bit mux2to1_8bit_2 (.A(IN1), .B(IN3), .S(S[1]), .F(mux2to1_8bit_2_f));
  MUX2to1_8bit mux2to1_8bit_3 (.A(mux2to1_8bit_1_f), .B(mux2to1_8bit_2_f), .S(S[0]), .F(MUX_out));

  // Notes on the sheet:
  //   (C input)
  //   (B input)
  //   (D input)
  //   (F)
endmodule

module MUX8to1_8bit (
  input  [7:0] IN0,
  input  [7:0] IN2,
  input  [7:0] IN1,
  input  [7:0] IN3,
  input  [7:0] IN4,
  input  [7:0] IN6,
  input  [7:0] IN5,
  input  [7:0] IN7,
  input  [2:0] S,
  output [7:0] F
);

  wire [7:0] mux4to1_8bit_1_mux_out, mux4to1_8bit_2_mux_out;

  MUX4to1_8bit mux4to1_8bit_1 (
    .IN0(IN0), .IN2(IN2), .IN1(IN1), .IN3(IN3), .S(S[1:0]), .MUX_out(mux4to1_8bit_1_mux_out));
  MUX4to1_8bit mux4to1_8bit_2 (
    .IN0(IN4), .IN2(IN6), .IN1(IN5), .IN3(IN7), .S(S[1:0]), .MUX_out(mux4to1_8bit_2_mux_out));
  MUX2to1_8bit mux2to1_8bit_1 (.A(mux4to1_8bit_1_mux_out), .B(mux4to1_8bit_2_mux_out), .S(S[2]), .F(F));

  // Notes on the sheet:
  //   Joshua Cox
endmodule

module MUX2to1_16bit (
  input  [15:0] A,
  input  [15:0] B,
  input  in_3,
  output [15:0] out_4
);

  MUX2to1_8bit mux2to1_8bit_1 (.A(A[7:0]), .B(B[7:0]), .S(in_3), .F(out_4[7:0]));
  MUX2to1_8bit mux2to1_8bit_2 (.A(A[15:8]), .B(B[15:8]), .S(in_3), .F(out_4[15:8]));
endmodule

module MUX4to1_16bit (
  input  [15:0] IN0,
  input  [15:0] IN1,
  input  [15:0] IN2,
  input  [15:0] IN3,
  input  [1:0] in_5,
  output [15:0] F
);

  wire [15:0] mux2to1_16bit_1_out_4, mux2to1_16bit_2_out_4;

  MUX2to1_16bit mux2to1_16bit_1 (.A(IN0), .B(IN2), .in_3(in_5[1]), .out_4(mux2to1_16bit_1_out_4));
  MUX2to1_16bit mux2to1_16bit_2 (.A(IN1), .B(IN3), .in_3(in_5[1]), .out_4(mux2to1_16bit_2_out_4));
  MUX2to1_16bit mux2to1_16bit_3 (.A(mux2to1_16bit_1_out_4), .B(mux2to1_16bit_2_out_4), .in_3(in_5[0]), .out_4(F));
endmodule

module MUX8to1_16bit (
  input  [15:0] IN0,
  input  [15:0] IN1,
  input  [15:0] IN2,
  input  [15:0] IN3,
  input  [15:0] IN4,
  input  [15:0] IN5,
  input  [15:0] IN6,
  input  [15:0] IN7,
  input  [2:0] in_9,
  output [15:0] out_10
);

  wire [15:0] mux4to1_16bit_1_f, mux4to1_16bit_2_f;

  MUX4to1_16bit mux4to1_16bit_1 (.IN0(IN0), .IN1(IN1), .IN2(IN2), .IN3(IN3), .in_5(in_9[1:0]), .F(mux4to1_16bit_1_f));
  MUX4to1_16bit mux4to1_16bit_2 (.IN0(IN4), .IN1(IN5), .IN2(IN6), .IN3(IN7), .in_5(in_9[1:0]), .F(mux4to1_16bit_2_f));
  MUX2to1_16bit mux2to1_16bit_1 (.A(mux4to1_16bit_1_f), .B(mux4to1_16bit_2_f), .in_3(in_9[2]), .out_4(out_10));
endmodule

module MUX16to1_16bit (
  input  [15:0] IN0,
  input  [15:0] IN1,
  input  [15:0] IN2,
  input  [15:0] IN3,
  input  [15:0] IN4,
  input  [15:0] IN5,
  input  [15:0] IN6,
  input  [15:0] IN7,
  input  [15:0] IN8,
  input  [15:0] IN9,
  input  [15:0] INA,
  input  [15:0] INB,
  input  [15:0] INC,
  input  [15:0] IND,
  input  [15:0] INE,
  input  [15:0] INF,
  input  [3:0] in_17,
  output [15:0] out_18
);

  wire [15:0] mux8to1_16bit_1_out_10, mux8to1_16bit_2_out_10;

  MUX8to1_16bit mux8to1_16bit_1 (
    .IN0(IN0), .IN1(IN1), .IN2(IN2), .IN3(IN3), .IN4(IN4), .IN5(IN5), .IN6(IN6), .IN7(IN7),
    .in_9(in_17[2:0]), .out_10(mux8to1_16bit_1_out_10));
  MUX8to1_16bit mux8to1_16bit_2 (
    .IN0(IN8), .IN1(IN9), .IN2(INA), .IN3(INB), .IN4(INC), .IN5(IND), .IN6(INE), .IN7(INF),
    .in_9(in_17[2:0]), .out_10(mux8to1_16bit_2_out_10));
  MUX2to1_16bit mux2to1_16bit_1 (
    .A(mux8to1_16bit_1_out_10), .B(mux8to1_16bit_2_out_10), .in_3(in_17[3]), .out_4(out_18));
endmodule

module AND_16bit (
  input  [15:0] in_1,
  input  [15:0] in_2,
  output [15:0] out_3
);

  AND_8bit and_8bit_1 (.A(in_1[7:0]), .B(in_2[7:0]), .out_3(out_3[7:0]));
  AND_8bit and_8bit_2 (.A(in_1[15:8]), .B(in_2[15:8]), .out_3(out_3[15:8]));
endmodule

module OR_16bit (
  input  [15:0] in_1,
  input  [15:0] in_2,
  output [15:0] out_3
);

  OR_8bit or_8bit_1 (.A(in_1[7:0]), .B(in_2[7:0]), .out_3(out_3[7:0]));
  OR_8bit or_8bit_2 (.A(in_1[15:8]), .B(in_2[15:8]), .out_3(out_3[15:8]));
endmodule

module XOR_16bit (
  input  [15:0] in_1,
  input  [15:0] in_2,
  output [15:0] out_3
);

  XOR_8bit xor_8bit_1 (.A(in_1[7:0]), .B(in_2[7:0]), .out_3(out_3[7:0]));
  XOR_8bit xor_8bit_2 (.A(in_1[15:8]), .B(in_2[15:8]), .out_3(out_3[15:8]));
endmodule

module ADD_16bit (
  input  [15:0] A,
  input  [15:0] B,
  input  Cin,
  output [15:0] ADD16,
  output Cout
);

  wire add_8bit_1_cout;

  ADD_8bit add_8bit_1 (.A(A[7:0]), .B(B[7:0]), .Cin(Cin), .ADD8(ADD16[7:0]), .Cout(add_8bit_1_cout));
  ADD_8bit add_8bit_2 (.A(A[15:8]), .B(B[15:8]), .Cin(add_8bit_1_cout), .ADD8(ADD16[15:8]), .Cout(Cout));
endmodule

module Invert_16bit (
  input  [15:0] in_1,
  output [15:0] out_2
);

  not not_1 (out_2[0], in_1[0]);
  not not_2 (out_2[1], in_1[1]);
  not not_3 (out_2[2], in_1[2]);
  not not_4 (out_2[3], in_1[3]);
  not not_5 (out_2[4], in_1[4]);
  not not_6 (out_2[5], in_1[5]);
  not not_7 (out_2[6], in_1[6]);
  not not_8 (out_2[7], in_1[7]);
  not not_9 (out_2[8], in_1[8]);
  not not_10 (out_2[9], in_1[9]);
  not not_11 (out_2[10], in_1[10]);
  not not_12 (out_2[11], in_1[11]);
  not not_13 (out_2[12], in_1[12]);
  not not_14 (out_2[13], in_1[13]);
  not not_15 (out_2[14], in_1[14]);
  not not_16 (out_2[15], in_1[15]);
endmodule

module LSR_16bit (
  input  [15:0] A,
  output [15:0] F,
  output Lost
);


  assign F = {1'b0, A[15:1]};
  assign Lost = A[0];
endmodule

module LSL_16bit (
  input  [15:0] A,
  output [15:0] F,
  output Lost
);


  assign F = {A[14:0], 1'b0};
  assign Lost = A[15];
endmodule

module Equivalence_16bit (
  input  [15:0] A,
  input  [15:0] B,
  output Less,
  output Equal,
  output Greater
);

  wire and_2_out, and_3_out, equivalence_8bit_1_equal, equivalence_8bit_1_greater, equivalence_8bit_1_less,
       equivalence_8bit_2_equal, equivalence_8bit_2_greater, equivalence_8bit_2_less;

  Equivalence_8bit equivalence_8bit_1 (
    .A(A[7:0]), .B(B[7:0]), .Less(equivalence_8bit_1_less), .Equal(equivalence_8bit_1_equal),
    .Greater(equivalence_8bit_1_greater));
  Equivalence_8bit equivalence_8bit_2 (
    .A(A[15:8]), .B(B[15:8]), .Less(equivalence_8bit_2_less), .Equal(equivalence_8bit_2_equal),
    .Greater(equivalence_8bit_2_greater));
  and and_1 (Equal, equivalence_8bit_1_equal, equivalence_8bit_2_equal);
  and and_2 (and_2_out, equivalence_8bit_1_less, equivalence_8bit_2_equal);
  and and_3 (and_3_out, equivalence_8bit_1_greater, equivalence_8bit_2_equal);
  or or_1 (Less, and_2_out, equivalence_8bit_2_less);
  or or_2 (Greater, and_3_out, equivalence_8bit_2_greater);
endmodule

module Equivalence_1bit (
  input  in_1,
  input  in_2,
  output Less,
  output Equal,
  output Greater
);

  wire not_1_out, not_2_out;

  not not_1 (not_1_out, in_1);
  not not_2 (not_2_out, in_2);
  and and_1 (Less, not_1_out, in_2);
  and and_2 (Greater, not_2_out, in_1);
  nor nor_1 (Equal, Less, Greater);
endmodule

module Equivalence_4bit (
  input  [3:0] A,
  input  [3:0] B,
  output Less,
  output Equal,
  output Greater
);

  wire and_2_out, and_3_out, and_4_out, and_5_out, and_6_out, and_7_out, equivalence_1bit_1_equal,
       equivalence_1bit_1_greater, equivalence_1bit_1_less, equivalence_1bit_2_equal,
       equivalence_1bit_2_greater, equivalence_1bit_2_less, equivalence_1bit_3_equal,
       equivalence_1bit_3_greater, equivalence_1bit_3_less, equivalence_1bit_4_equal,
       equivalence_1bit_4_greater, equivalence_1bit_4_less;

  Equivalence_1bit equivalence_1bit_1 (
    .in_1(A[0]), .in_2(B[0]), .Less(equivalence_1bit_1_less), .Equal(equivalence_1bit_1_equal),
    .Greater(equivalence_1bit_1_greater));
  Equivalence_1bit equivalence_1bit_2 (
    .in_1(A[1]), .in_2(B[1]), .Less(equivalence_1bit_2_less), .Equal(equivalence_1bit_2_equal),
    .Greater(equivalence_1bit_2_greater));
  Equivalence_1bit equivalence_1bit_3 (
    .in_1(A[2]), .in_2(B[2]), .Less(equivalence_1bit_3_less), .Equal(equivalence_1bit_3_equal),
    .Greater(equivalence_1bit_3_greater));
  Equivalence_1bit equivalence_1bit_4 (
    .in_1(A[3]), .in_2(B[3]), .Less(equivalence_1bit_4_less), .Equal(equivalence_1bit_4_equal),
    .Greater(equivalence_1bit_4_greater));
  and and_1 (Equal, equivalence_1bit_1_equal, equivalence_1bit_2_equal, equivalence_1bit_3_equal, equivalence_1bit_4_equal);
  and and_2 (and_2_out, equivalence_1bit_1_less, equivalence_1bit_2_equal, equivalence_1bit_3_equal, equivalence_1bit_4_equal);
  and and_3 (and_3_out, equivalence_1bit_1_greater, equivalence_1bit_4_equal, equivalence_1bit_3_equal, equivalence_1bit_2_equal);
  and and_4 (and_4_out, equivalence_1bit_2_less, equivalence_1bit_3_equal, equivalence_1bit_4_equal);
  and and_5 (and_5_out, equivalence_1bit_2_greater, equivalence_1bit_3_equal, equivalence_1bit_4_equal);
  and and_6 (and_6_out, equivalence_1bit_3_less, equivalence_1bit_4_equal);
  and and_7 (and_7_out, equivalence_1bit_3_greater, equivalence_1bit_4_equal);
  or or_1 (Less, and_2_out, and_4_out, and_6_out, equivalence_1bit_4_less);
  or or_2 (Greater, and_3_out, and_5_out, and_7_out, equivalence_1bit_4_greater);
endmodule

module Equivalence_8bit (
  input  [7:0] A,
  input  [7:0] B,
  output Less,
  output Equal,
  output Greater
);

  wire and_2_out, and_3_out, equivalence_4bit_1_equal, equivalence_4bit_1_greater, equivalence_4bit_1_less,
       equivalence_4bit_2_equal, equivalence_4bit_2_greater, equivalence_4bit_2_less;

  Equivalence_4bit equivalence_4bit_1 (
    .A(A[3:0]), .B(B[3:0]), .Less(equivalence_4bit_1_less), .Equal(equivalence_4bit_1_equal),
    .Greater(equivalence_4bit_1_greater));
  Equivalence_4bit equivalence_4bit_2 (
    .A(A[7:4]), .B(B[7:4]), .Less(equivalence_4bit_2_less), .Equal(equivalence_4bit_2_equal),
    .Greater(equivalence_4bit_2_greater));
  and and_1 (Equal, equivalence_4bit_1_equal, equivalence_4bit_2_equal);
  and and_2 (and_2_out, equivalence_4bit_1_less, equivalence_4bit_2_equal);
  and and_3 (and_3_out, equivalence_4bit_1_greater, equivalence_4bit_2_equal);
  or or_1 (Less, and_2_out, equivalence_4bit_2_less);
  or or_2 (Greater, and_3_out, equivalence_4bit_2_greater);
endmodule

module ZeroCheck_4bit (
  input  [3:0] A,
  output Zero
);

  and and_1 (Zero, ~A[0], ~A[1], ~A[2], ~A[3]);  // AND_Gate
endmodule

module CheckZero_16bit (
  input  [15:0] A,
  output Zero
);

  wire zerocheck_4bit_1_zero, zerocheck_4bit_2_zero, zerocheck_4bit_3_zero, zerocheck_4bit_4_zero;

  ZeroCheck_4bit zerocheck_4bit_1 (.A(A[3:0]), .Zero(zerocheck_4bit_1_zero));
  ZeroCheck_4bit zerocheck_4bit_2 (.A(A[7:4]), .Zero(zerocheck_4bit_2_zero));
  ZeroCheck_4bit zerocheck_4bit_3 (.A(A[11:8]), .Zero(zerocheck_4bit_3_zero));
  ZeroCheck_4bit zerocheck_4bit_4 (.A(A[15:12]), .Zero(zerocheck_4bit_4_zero));
  and and_1 (Zero, zerocheck_4bit_1_zero, zerocheck_4bit_2_zero, zerocheck_4bit_3_zero, zerocheck_4bit_4_zero);
endmodule

module Multiplier_4bit (
  input  [3:0] A,
  input  [3:0] B,
  output [7:0] F
);

  wire add_4bit_1_cout, add_4bit_2_cout, add_4bit_3_cout, lsr_4bit_1_lost, lsr_4bit_2_lost;
  wire [1:0] add_4bit_1_add4;
  wire [3:0] add_4bit_2_add4, and_1_4bit_1_f, and_1_4bit_2_f, and_1_4bit_3_f, and_1_4bit_4_f,
       lsr_4bit_1_lsr4, lsr_4bit_2_lsr4;
  wire [3:2] full_adder_1_s;

  AND_1_4bit and_1_4bit_1 (.in_1(A), .in_2(B[0]), .F(and_1_4bit_1_f));
  AND_1_4bit and_1_4bit_2 (.in_1(A), .in_2(B[1]), .F(and_1_4bit_2_f));
  AND_1_4bit and_1_4bit_3 (.in_1(A), .in_2(B[2]), .F(and_1_4bit_3_f));
  AND_1_4bit and_1_4bit_4 (.in_1(A), .in_2(B[3]), .F(and_1_4bit_4_f));
  LSR_4bit lsr_4bit_1 (.A(and_1_4bit_2_f), .LSR4(lsr_4bit_1_lsr4), .Lost(lsr_4bit_1_lost));
  LSR_4bit lsr_4bit_2 (.A(and_1_4bit_4_f), .LSR4(lsr_4bit_2_lsr4), .Lost(lsr_4bit_2_lost));
  Add_4bit add_4bit_1 (
    .A(and_1_4bit_1_f), .B(lsr_4bit_1_lsr4), .ADD4({add_4bit_1_add4, F[1:0]}), .Cout(add_4bit_1_cout));  // open: Cin
  Add_4bit add_4bit_2 (
    .A(and_1_4bit_3_f), .B(lsr_4bit_2_lsr4), .ADD4(add_4bit_2_add4), .Cout(add_4bit_2_cout));  // open: Cin
  Full_Adder full_adder_1 (
    .A(add_4bit_1_cout), .B(lsr_4bit_1_lost), .S(full_adder_1_s[2]), .Cout(full_adder_1_s[3]));  // open: Cin
  Add_4bit add_4bit_3 (
    .A({full_adder_1_s, add_4bit_1_add4}), .B(add_4bit_2_add4), .ADD4(F[5:2]), .Cout(add_4bit_3_cout));  // open: Cin
  Full_Adder full_adder_2 (.A(add_4bit_2_cout), .B(lsr_4bit_2_lost), .Cin(add_4bit_3_cout), .S(F[6]), .Cout(F[7]));
endmodule

module AND_1_4bit (
  input  [3:0] in_1,
  input  in_2,
  output [3:0] F
);

  and and_1 (F[0], in_1[0], in_2);
  and and_2 (F[1], in_1[1], in_2);
  and and_3 (F[2], in_1[2], in_2);
  and and_4 (F[3], in_1[3], in_2);
endmodule

module Multiplier_8bit (
  input  [7:0] A,
  input  [7:0] B,
  output [15:0] F
);

  wire [7:0] multiplier_4bit_1_f, multiplier_4bit_2_f, multiplier_4bit_3_f, multiplier_4bit_4_f;
  wire [15:0] add_16bit_1_add16, add_16bit_2_add16;

  Multiplier_4bit multiplier_4bit_1 (.A(A[3:0]), .B(B[3:0]), .F(multiplier_4bit_1_f));
  Multiplier_4bit multiplier_4bit_2 (.A(A[3:0]), .B(B[7:4]), .F(multiplier_4bit_2_f));
  Multiplier_4bit multiplier_4bit_3 (.A(A[7:4]), .B(B[3:0]), .F(multiplier_4bit_3_f));
  Multiplier_4bit multiplier_4bit_4 (.A(A[7:4]), .B(B[7:4]), .F(multiplier_4bit_4_f));
  ADD_16bit add_16bit_1 (
    .A({{8{1'b0}}, multiplier_4bit_1_f}), .B({4'b0000, multiplier_4bit_2_f, 4'b0000}),
    .ADD16(add_16bit_1_add16));  // open: Cin, Cout
  ADD_16bit add_16bit_2 (
    .A({4'b0000, multiplier_4bit_3_f, 4'b0000}), .B({multiplier_4bit_4_f, {8{1'b0}}}),
    .ADD16(add_16bit_2_add16));  // open: Cin, Cout
  ADD_16bit add_16bit_3 (.A(add_16bit_1_add16), .B(add_16bit_2_add16), .ADD16(F));  // open: Cin, Cout
endmodule

module Multiplier_16bit (
  input  [15:0] A,
  input  [15:0] B,
  output [31:0] F
);

  wire [15:0] multiplier_8bit_1_f, multiplier_8bit_2_f, multiplier_8bit_3_f, multiplier_8bit_4_f;
  wire [31:0] add_32bit_1_add32, add_32bit_2_add32;

  Multiplier_8bit multiplier_8bit_1 (.A(A[7:0]), .B(B[7:0]), .F(multiplier_8bit_1_f));
  Multiplier_8bit multiplier_8bit_2 (.A(A[7:0]), .B(B[15:8]), .F(multiplier_8bit_2_f));
  Multiplier_8bit multiplier_8bit_3 (.A(A[15:8]), .B(B[7:0]), .F(multiplier_8bit_3_f));
  Multiplier_8bit multiplier_8bit_4 (.A(A[15:8]), .B(B[15:8]), .F(multiplier_8bit_4_f));
  ADD_32bit add_32bit_1 (
    .A({{16{1'b0}}, multiplier_8bit_1_f}), .B({{8{1'b0}}, multiplier_8bit_2_f, {8{1'b0}}}),
    .ADD32(add_32bit_1_add32));  // open: Cin, Sub, Cout
  ADD_32bit add_32bit_2 (
    .A({{8{1'b0}}, multiplier_8bit_3_f, {8{1'b0}}}), .B({multiplier_8bit_4_f, {16{1'b0}}}),
    .ADD32(add_32bit_2_add32));  // open: Cin, Sub, Cout
  ADD_32bit add_32bit_3 (.A(add_32bit_1_add32), .B(add_32bit_2_add32), .ADD32(F));  // open: Cin, Sub, Cout
endmodule

module ADD_32bit (
  input  [31:0] A,
  input  [31:0] B,
  input  Cin,
  input  Sub,
  output [31:0] ADD32,
  output Cout
);

  wire add_16bit_1_cout, add_16bit_2_cout, xor_1_out;
  wire [15:0] mux2to1_32bit_1_out_4, mux2to1_32bit_1_out_4_2;
  wire [31:0] invert_32bit_1_out_2;

  xor xor_1 (xor_1_out, Cin, Sub);
  Invert_32bit invert_32bit_1 (.A(B), .out_2(invert_32bit_1_out_2));
  ADD_16bit add_16bit_1 (
    .A(A[15:0]), .B(mux2to1_32bit_1_out_4), .Cin(xor_1_out), .ADD16(ADD32[15:0]), .Cout(add_16bit_1_cout));
  ADD_16bit add_16bit_2 (
    .A(A[31:16]), .B(mux2to1_32bit_1_out_4_2), .Cin(add_16bit_1_cout), .ADD16(ADD32[31:16]),
    .Cout(add_16bit_2_cout));
  MUX2to1_32bit mux2to1_32bit_1 (
    .A(B), .B(invert_32bit_1_out_2), .in_3(Sub), .out_4({mux2to1_32bit_1_out_4_2, mux2to1_32bit_1_out_4}));
  xor xor_2 (Cout, add_16bit_2_cout, Sub);
endmodule

module Invert_32bit (
  input  [31:0] A,
  output [31:0] out_2
);

  Invert_16bit invert_16bit_1 (.in_1(A[15:0]), .out_2(out_2[15:0]));
  Invert_16bit invert_16bit_2 (.in_1(A[31:16]), .out_2(out_2[31:16]));
endmodule

module MUX2to1_32bit (
  input  [31:0] A,
  input  [31:0] B,
  input  in_3,
  output [31:0] out_4
);

  MUX2to1_16bit mux2to1_16bit_1 (.A(A[15:0]), .B(B[15:0]), .in_3(in_3), .out_4(out_4[15:0]));
  MUX2to1_16bit mux2to1_16bit_2 (.A(A[31:16]), .B(B[31:16]), .in_3(in_3), .out_4(out_4[31:16]));
endmodule

module MUX4to1_32bit (
  input  [31:0] IN0,
  input  [31:0] IN1,
  input  [31:0] IN2,
  input  [31:0] IN3,
  input  [1:0] in_5,
  output [31:0] F
);

  wire [31:0] mux2to1_32bit_1_out_4, mux2to1_32bit_2_out_4;

  MUX2to1_32bit mux2to1_32bit_1 (.A(IN0), .B(IN2), .in_3(in_5[1]), .out_4(mux2to1_32bit_1_out_4));
  MUX2to1_32bit mux2to1_32bit_2 (.A(IN1), .B(IN3), .in_3(in_5[1]), .out_4(mux2to1_32bit_2_out_4));
  MUX2to1_32bit mux2to1_32bit_3 (.A(mux2to1_32bit_1_out_4), .B(mux2to1_32bit_2_out_4), .in_3(in_5[0]), .out_4(F));
endmodule

module MUX8to1_32bit (
  input  [31:0] IN0,
  input  [31:0] IN1,
  input  [31:0] IN2,
  input  [31:0] IN3,
  input  [31:0] IN4,
  input  [31:0] IN5,
  input  [31:0] IN6,
  input  [31:0] IN7,
  input  [2:0] in_9,
  output [31:0] out_10
);

  wire [31:0] mux4to1_32bit_1_f, mux4to1_32bit_2_f;

  MUX4to1_32bit mux4to1_32bit_1 (.IN0(IN0), .IN1(IN1), .IN2(IN2), .IN3(IN3), .in_5(in_9[1:0]), .F(mux4to1_32bit_1_f));
  MUX4to1_32bit mux4to1_32bit_2 (.IN0(IN4), .IN1(IN5), .IN2(IN6), .IN3(IN7), .in_5(in_9[1:0]), .F(mux4to1_32bit_2_f));
  MUX2to1_32bit mux2to1_32bit_1 (.A(mux4to1_32bit_1_f), .B(mux4to1_32bit_2_f), .in_3(in_9[2]), .out_4(out_10));
endmodule

module MUX16to1_32bit (
  input  [31:0] IN0,
  input  [31:0] IN1,
  input  [31:0] IN2,
  input  [31:0] IN3,
  input  [31:0] IN4,
  input  [31:0] IN5,
  input  [31:0] IN6,
  input  [31:0] IN7,
  input  [31:0] IN8,
  input  [31:0] IN9,
  input  [31:0] INA,
  input  [31:0] INB,
  input  [31:0] INC,
  input  [31:0] IND,
  input  [31:0] INE,
  input  [31:0] INF,
  input  [3:0] in_17,
  output [31:0] out_18
);

  wire [31:0] mux8to1_32bit_1_out_10, mux8to1_32bit_2_out_10;

  MUX8to1_32bit mux8to1_32bit_1 (
    .IN0(IN0), .IN1(IN1), .IN2(IN2), .IN3(IN3), .IN4(IN4), .IN5(IN5), .IN6(IN6), .IN7(IN7),
    .in_9(in_17[2:0]), .out_10(mux8to1_32bit_1_out_10));
  MUX8to1_32bit mux8to1_32bit_2 (
    .IN0(IN8), .IN1(IN9), .IN2(INA), .IN3(INB), .IN4(INC), .IN5(IND), .IN6(INE), .IN7(INF),
    .in_9(in_17[2:0]), .out_10(mux8to1_32bit_2_out_10));
  MUX2to1_32bit mux2to1_32bit_1 (
    .A(mux8to1_32bit_1_out_10), .B(mux8to1_32bit_2_out_10), .in_3(in_17[3]), .out_4(out_18));
endmodule

module AND_32bit (
  input  [31:0] in_1,
  input  [31:0] in_2,
  output [31:0] out_3
);

  AND_16bit and_16bit_1 (.in_1(in_1[15:0]), .in_2(in_2[15:0]), .out_3(out_3[15:0]));
  AND_16bit and_16bit_2 (.in_1(in_1[31:16]), .in_2(in_2[31:16]), .out_3(out_3[31:16]));
endmodule

module XOR_32bit (
  input  [31:0] A,
  input  [31:0] B,
  output [31:0] F
);

  XOR_16bit xor_16bit_1 (.in_1(A[15:0]), .in_2(B[15:0]), .out_3(F[15:0]));
  XOR_16bit xor_16bit_2 (.in_1(A[31:16]), .in_2(B[31:16]), .out_3(F[31:16]));
endmodule

module OR_32bit (
  input  [31:0] in_1,
  input  [31:0] in_2,
  output [31:0] out_3
);

  OR_16bit or_16bit_1 (.in_1(in_1[15:0]), .in_2(in_2[15:0]), .out_3(out_3[15:0]));
  OR_16bit or_16bit_2 (.in_1(in_1[31:16]), .in_2(in_2[31:16]), .out_3(out_3[31:16]));
endmodule

module Equivalence_32bit (
  input  [31:0] A,
  input  [31:0] B,
  output Less,
  output Equal,
  output Greater
);

  wire and_2_out, and_3_out, equivalence_16bit_1_equal, equivalence_16bit_1_greater,
       equivalence_16bit_1_less, equivalence_16bit_2_equal, equivalence_16bit_2_greater,
       equivalence_16bit_2_less;

  Equivalence_16bit equivalence_16bit_1 (
    .A(A[15:0]), .B(B[15:0]), .Less(equivalence_16bit_1_less), .Equal(equivalence_16bit_1_equal),
    .Greater(equivalence_16bit_1_greater));
  Equivalence_16bit equivalence_16bit_2 (
    .A(A[31:16]), .B(B[31:16]), .Less(equivalence_16bit_2_less), .Equal(equivalence_16bit_2_equal),
    .Greater(equivalence_16bit_2_greater));
  and and_1 (Equal, equivalence_16bit_1_equal, equivalence_16bit_2_equal);
  and and_2 (and_2_out, equivalence_16bit_1_less, equivalence_16bit_2_equal);
  and and_3 (and_3_out, equivalence_16bit_1_greater, equivalence_16bit_2_equal);
  or or_1 (Less, and_2_out, equivalence_16bit_2_less);
  or or_2 (Greater, and_3_out, equivalence_16bit_2_greater);
endmodule

module LSR_32bit (
  input  [31:0] A,
  output [31:0] F,
  output Lost
);


  assign F = {1'b0, A[31:1]};
  assign Lost = A[0];
endmodule

module LSL_32bit (
  input  [31:0] A,
  output [31:0] out_2,
  output Lost
);


  assign Lost = A[31];
  assign out_2 = {A[30:0], 1'b0};
endmodule

module ZeroCheck_32bit (
  input  [31:0] A,
  output ZERO
);

  wire checkzero_16bit_1_zero, checkzero_16bit_2_zero;

  CheckZero_16bit checkzero_16bit_1 (.A(A[15:0]), .Zero(checkzero_16bit_1_zero));
  CheckZero_16bit checkzero_16bit_2 (.A(A[31:16]), .Zero(checkzero_16bit_2_zero));
  and and_1 (ZERO, checkzero_16bit_1_zero, checkzero_16bit_2_zero);
endmodule

module Invert_64bit (
  input  [63:0] A,
  output [63:0] out_2
);

  Invert_32bit invert_32bit_1 (.A(A[31:0]), .out_2(out_2[31:0]));
  Invert_32bit invert_32bit_2 (.A(A[63:32]), .out_2(out_2[63:32]));
endmodule

module ADD_64bit (
  input  [63:0] A,
  input  [63:0] B,
  input  Cin,
  input  Sub,
  output [63:0] ADD64,
  output Cout
);

  wire add_32bit_1_cout, add_32bit_2_cout, xor_1_out;
  wire [31:0] mux2to1_64bit_1_out_4, mux2to1_64bit_1_out_4_2;
  wire [63:0] invert_64bit_1_out_2;

  xor xor_1 (xor_1_out, Cin, Sub);
  Invert_64bit invert_64bit_1 (.A(B), .out_2(invert_64bit_1_out_2));
  ADD_32bit add_32bit_1 (
    .A(A[31:0]), .B(mux2to1_64bit_1_out_4), .Cin(xor_1_out), .ADD32(ADD64[31:0]), .Cout(add_32bit_1_cout));  // open: Sub
  MUX2to1_64bit mux2to1_64bit_1 (
    .A(B), .B(invert_64bit_1_out_2), .in_3(Sub), .out_4({mux2to1_64bit_1_out_4_2, mux2to1_64bit_1_out_4}));
  ADD_32bit add_32bit_2 (
    .A(A[63:32]), .B(mux2to1_64bit_1_out_4_2), .Cin(add_32bit_1_cout), .ADD32(ADD64[63:32]),
    .Cout(add_32bit_2_cout));  // open: Sub
  xor xor_2 (Cout, add_32bit_2_cout, Sub);
endmodule

module MUX2to1_64bit (
  input  [63:0] A,
  input  [63:0] B,
  input  in_3,
  output [63:0] out_4
);

  MUX2to1_32bit mux2to1_32bit_1 (.A(A[31:0]), .B(B[31:0]), .in_3(in_3), .out_4(out_4[31:0]));
  MUX2to1_32bit mux2to1_32bit_2 (.A(A[63:32]), .B(B[63:32]), .in_3(in_3), .out_4(out_4[63:32]));
endmodule

module MUX4to1_64bit (
  input  [63:0] IN0,
  input  [63:0] IN1,
  input  [63:0] IN2,
  input  [63:0] IN3,
  input  [1:0] in_5,
  output [63:0] F
);

  wire [63:0] mux2to1_64bit_1_out_4, mux2to1_64bit_2_out_4;

  MUX2to1_64bit mux2to1_64bit_1 (.A(IN0), .B(IN2), .in_3(in_5[1]), .out_4(mux2to1_64bit_1_out_4));
  MUX2to1_64bit mux2to1_64bit_2 (.A(IN1), .B(IN3), .in_3(in_5[1]), .out_4(mux2to1_64bit_2_out_4));
  MUX2to1_64bit mux2to1_64bit_3 (.A(mux2to1_64bit_1_out_4), .B(mux2to1_64bit_2_out_4), .in_3(in_5[0]), .out_4(F));
endmodule

module MUX8to1_64bit (
  input  [63:0] IN0,
  input  [63:0] IN1,
  input  [63:0] IN2,
  input  [63:0] IN3,
  input  [63:0] IN4,
  input  [63:0] IN5,
  input  [63:0] IN6,
  input  [63:0] IN7,
  input  [2:0] in_9,
  output [63:0] out_10
);

  wire [63:0] mux4to1_64bit_1_f, mux4to1_64bit_2_f;

  MUX4to1_64bit mux4to1_64bit_1 (.IN0(IN0), .IN1(IN1), .IN2(IN2), .IN3(IN3), .in_5(in_9[1:0]), .F(mux4to1_64bit_1_f));
  MUX4to1_64bit mux4to1_64bit_2 (.IN0(IN4), .IN1(IN5), .IN2(IN6), .IN3(IN7), .in_5(in_9[1:0]), .F(mux4to1_64bit_2_f));
  MUX2to1_64bit mux2to1_64bit_1 (.A(mux4to1_64bit_1_f), .B(mux4to1_64bit_2_f), .in_3(in_9[2]), .out_4(out_10));
endmodule

module MUX16to1_64bit (
  input  [63:0] IN0,
  input  [63:0] IN1,
  input  [63:0] IN2,
  input  [63:0] IN3,
  input  [63:0] IN4,
  input  [63:0] IN5,
  input  [63:0] IN6,
  input  [63:0] IN7,
  input  [63:0] IN8,
  input  [63:0] IN9,
  input  [63:0] INA,
  input  [63:0] INB,
  input  [63:0] INC,
  input  [63:0] IND,
  input  [63:0] INE,
  input  [63:0] INF,
  input  [3:0] in_17,
  output [63:0] out_18
);

  wire [63:0] mux8to1_64bit_1_out_10, mux8to1_64bit_2_out_10;

  MUX8to1_64bit mux8to1_64bit_1 (
    .IN0(IN0), .IN1(IN1), .IN2(IN2), .IN3(IN3), .IN4(IN4), .IN5(IN5), .IN6(IN6), .IN7(IN7),
    .in_9(in_17[2:0]), .out_10(mux8to1_64bit_1_out_10));
  MUX8to1_64bit mux8to1_64bit_2 (
    .IN0(IN8), .IN1(IN9), .IN2(INA), .IN3(INB), .IN4(INC), .IN5(IND), .IN6(INE), .IN7(INF),
    .in_9(in_17[2:0]), .out_10(mux8to1_64bit_2_out_10));
  MUX2to1_64bit mux2to1_64bit_1 (
    .A(mux8to1_64bit_1_out_10), .B(mux8to1_64bit_2_out_10), .in_3(in_17[3]), .out_4(out_18));
endmodule

module Multiplier_32bit (
  input  [31:0] A,
  input  [31:0] B,
  output [63:0] F
);

  wire [31:0] multiplier_16bit_1_f, multiplier_16bit_2_f, multiplier_16bit_3_f, multiplier_16bit_4_f;
  wire [63:0] add_64bit_1_add64, add_64bit_2_add64;

  Multiplier_16bit multiplier_16bit_1 (.A(A[15:0]), .B(B[15:0]), .F(multiplier_16bit_1_f));
  Multiplier_16bit multiplier_16bit_2 (.A(A[15:0]), .B(B[31:16]), .F(multiplier_16bit_2_f));
  Multiplier_16bit multiplier_16bit_3 (.A(A[31:16]), .B(B[15:0]), .F(multiplier_16bit_3_f));
  Multiplier_16bit multiplier_16bit_4 (.A(A[31:16]), .B(B[31:16]), .F(multiplier_16bit_4_f));
  ADD_64bit add_64bit_1 (
    .A({{32{1'b0}}, multiplier_16bit_1_f}), .B({{16{1'b0}}, multiplier_16bit_2_f, {16{1'b0}}}),
    .ADD64(add_64bit_1_add64));  // open: Cin, Sub, Cout
  ADD_64bit add_64bit_2 (
    .A({{16{1'b0}}, multiplier_16bit_3_f, {16{1'b0}}}), .B({multiplier_16bit_4_f, {32{1'b0}}}),
    .ADD64(add_64bit_2_add64));  // open: Cin, Sub, Cout
  ADD_64bit add_64bit_3 (.A(add_64bit_1_add64), .B(add_64bit_2_add64), .ADD64(F));  // open: Cin, Sub, Cout
endmodule

module HalfAdd_128bit (
  input  [63:0] Al,
  input  [63:0] Ah,
  input  [63:0] Bl,
  input  [63:0] Bh,
  input  Cin,
  output [63:0] ADD128_L,
  output [63:0] ADD128_H,
  output Cout
);

  wire add_64bit_1_cout;

  ADD_64bit add_64bit_1 (.A(Al), .B(Bl), .Cin(Cin), .ADD64(ADD128_L), .Cout(add_64bit_1_cout));  // open: Sub
  ADD_64bit add_64bit_2 (.A(Ah), .B(Bh), .Cin(add_64bit_1_cout), .ADD64(ADD128_H), .Cout(Cout));  // open: Sub
endmodule

module Multiplier_64bit (
  input  [31:0] A,
  input  [31:0] B,
  output [63:0] F
);

  wire [31:0] multiplier_32bit_3_p3, multiplier_32bit_4_p3, multiplier_32bit_5_p3, undriven;
  wire [63:0] add_64bit_1_add64, add_64bit_2_add64;

  Multiplier_32bit multiplier_32bit_1 ();  // open: A, B, F
  Multiplier_32bit multiplier_32bit_2 ();  // open: A, B, F
  // Multiplier_32bit multiplier_32bit_3: pin names not known; wires that end beside it: A[15:0], B[15:0], multiplier_32bit_3_p3
  // Multiplier_32bit multiplier_32bit_4: pin names not known; wires that end beside it: A[15:0], B[31:16], multiplier_32bit_4_p3
  // Multiplier_32bit multiplier_32bit_5: pin names not known; wires that end beside it: A[31:16], B[15:0], multiplier_32bit_5_p3
  ADD_64bit add_64bit_1 (
    .A({{32{1'b0}}, multiplier_32bit_3_p3}), .B({{16{1'b0}}, multiplier_32bit_4_p3, {16{1'b0}}}),
    .ADD64(add_64bit_1_add64));  // open: Cin, Sub, Cout
  ADD_64bit add_64bit_2 (
    .A({{16{1'b0}}, multiplier_32bit_5_p3, {16{1'b0}}}), .B({undriven, {32{1'b0}}}), .ADD64(add_64bit_2_add64));  // open: Cin, Sub, Cout
  ADD_64bit add_64bit_3 (.A(add_64bit_1_add64), .B(add_64bit_2_add64), .ADD64(F));  // open: Cin, Sub, Cout
endmodule

module ALU_32bit (
  input  [31:0] A,
  input  [31:0] B,
  input  Cin,
  input  [3:0] S,
  output [31:0] ALU_out,
  output [31:0] ALU_Upper_out,
  output Cout,
  output Zero,
  output Less,
  output Equal,
  output Greater
);

  wire [31:0] add_32bit_1_add32, and_32bit_1_out_3, invert_32bit_1_out_2, multiplier_32bit_1_f,
       or_32bit_1_out_3, v_lsl_32bit_1_out_3, v_lsr_32bit_1_out_3, xor_32bit_1_f;

  XOR_32bit xor_32bit_1 (.A(A), .B(B), .F(xor_32bit_1_f));
  OR_32bit or_32bit_1 (.in_1(A), .in_2(B), .out_3(or_32bit_1_out_3));
  AND_32bit and_32bit_1 (.in_1(A), .in_2(B), .out_3(and_32bit_1_out_3));
  ADD_32bit add_32bit_1 (.A(A), .B(B), .Cin(Cin), .Sub(S[2]), .ADD32(add_32bit_1_add32), .Cout(Cout));
  V_LSR_32bit v_lsr_32bit_1 (.in_1(A), .Shift(B[4:0]), .out_3(v_lsr_32bit_1_out_3));
  Invert_32bit invert_32bit_1 (.A(A), .out_2(invert_32bit_1_out_2));
  V_LSL_32bit v_lsl_32bit_1 (.in_1(A), .Shift(B[4:0]), .out_3(v_lsl_32bit_1_out_3));
  Multiplier_32bit multiplier_32bit_1 (.A(A), .B(B), .F({ALU_Upper_out, multiplier_32bit_1_f}));
  Equivalence_32bit equivalence_32bit_1 (.A(A), .B(B), .Less(Less), .Equal(Equal), .Greater(Greater));
  MUX16to1_32bit mux16to1_32bit_1 (
    .IN0(xor_32bit_1_f), .IN1(or_32bit_1_out_3), .IN2(and_32bit_1_out_3), .IN3(add_32bit_1_add32),
    .IN4(v_lsr_32bit_1_out_3), .IN5(invert_32bit_1_out_2), .IN6(v_lsl_32bit_1_out_3),
    .IN7(add_32bit_1_add32), .IN8(multiplier_32bit_1_f), .in_17(S), .out_18(ALU_out));  // open: IN9, INA, INB, INC, IND, INE, INF
  ZeroCheck_32bit zerocheck_32bit_1 (.A(ALU_out), .ZERO(Zero));

  // Notes on the sheet:
  //   Joshua Cox
endmodule

module Register_32bit (
  input  [31:0] Din,
  input  Write,
  input  Clk,
  input  Reset,
  output [31:0] Dout
);

  wire multiplexer_1_out, multiplexer_2_out, multiplexer_3_out, multiplexer_4_out, multiplexer_5_out,
       multiplexer_6_out, multiplexer_7_out, multiplexer_8_out, multiplexer_9_out, multiplexer_10_out,
       multiplexer_11_out, multiplexer_12_out, multiplexer_13_out, multiplexer_14_out, multiplexer_15_out,
       multiplexer_16_out, multiplexer_17_out, multiplexer_18_out, multiplexer_19_out, multiplexer_20_out,
       multiplexer_21_out, multiplexer_22_out, multiplexer_23_out, multiplexer_24_out, multiplexer_25_out,
       multiplexer_26_out, multiplexer_27_out, multiplexer_28_out, multiplexer_29_out, multiplexer_30_out,
       multiplexer_31_out, multiplexer_32_out;

  D_Flip_Flop d_ff_1 (.D(multiplexer_1_out), .clk(Clk), .Q(Dout[0]), .reset(Reset));  // open: Qn, preset
  Multiplexer multiplexer_1 (.in0(Dout[0]), .in1(Din[0]), .out(multiplexer_1_out), .sel(Write));
  D_Flip_Flop d_ff_2 (.D(multiplexer_2_out), .clk(Clk), .Q(Dout[8]), .reset(Reset));  // open: Qn, preset
  Multiplexer multiplexer_2 (.in0(Dout[8]), .in1(Din[8]), .out(multiplexer_2_out), .sel(Write));
  D_Flip_Flop d_ff_3 (.D(multiplexer_3_out), .clk(Clk), .Q(Dout[16]), .reset(Reset));  // open: Qn, preset
  Multiplexer multiplexer_3 (.in0(Dout[16]), .in1(Din[16]), .out(multiplexer_3_out), .sel(Write));
  D_Flip_Flop d_ff_4 (.D(multiplexer_4_out), .clk(Clk), .Q(Dout[24]), .reset(Reset));  // open: Qn, preset
  Multiplexer multiplexer_4 (.in0(Dout[24]), .in1(Din[24]), .out(multiplexer_4_out), .sel(Write));
  D_Flip_Flop d_ff_5 (.D(multiplexer_5_out), .clk(Clk), .Q(Dout[1]), .reset(Reset));  // open: Qn, preset
  Multiplexer multiplexer_5 (.in0(Dout[1]), .in1(Din[1]), .out(multiplexer_5_out), .sel(Write));
  D_Flip_Flop d_ff_6 (.D(multiplexer_6_out), .clk(Clk), .Q(Dout[9]), .reset(Reset));  // open: Qn, preset
  Multiplexer multiplexer_6 (.in0(Dout[9]), .in1(Din[9]), .out(multiplexer_6_out), .sel(Write));
  D_Flip_Flop d_ff_7 (.D(multiplexer_7_out), .clk(Clk), .Q(Dout[17]), .reset(Reset));  // open: Qn, preset
  Multiplexer multiplexer_7 (.in0(Dout[17]), .in1(Din[17]), .out(multiplexer_7_out), .sel(Write));
  D_Flip_Flop d_ff_8 (.D(multiplexer_8_out), .clk(Clk), .Q(Dout[25]), .reset(Reset));  // open: Qn, preset
  Multiplexer multiplexer_8 (.in0(Dout[25]), .in1(Din[25]), .out(multiplexer_8_out), .sel(Write));
  D_Flip_Flop d_ff_9 (.D(multiplexer_9_out), .clk(Clk), .Q(Dout[2]), .reset(Reset));  // open: Qn, preset
  Multiplexer multiplexer_9 (.in0(Dout[2]), .in1(Din[2]), .out(multiplexer_9_out), .sel(Write));
  D_Flip_Flop d_ff_10 (.D(multiplexer_10_out), .clk(Clk), .Q(Dout[10]), .reset(Reset));  // open: Qn, preset
  Multiplexer multiplexer_10 (.in0(Dout[10]), .in1(Din[10]), .out(multiplexer_10_out), .sel(Write));
  D_Flip_Flop d_ff_11 (.D(multiplexer_11_out), .clk(Clk), .Q(Dout[18]), .reset(Reset));  // open: Qn, preset
  Multiplexer multiplexer_11 (.in0(Dout[18]), .in1(Din[18]), .out(multiplexer_11_out), .sel(Write));
  D_Flip_Flop d_ff_12 (.D(multiplexer_12_out), .clk(Clk), .Q(Dout[26]), .reset(Reset));  // open: Qn, preset
  Multiplexer multiplexer_12 (.in0(Dout[26]), .in1(Din[26]), .out(multiplexer_12_out), .sel(Write));
  D_Flip_Flop d_ff_13 (.D(multiplexer_13_out), .clk(Clk), .Q(Dout[3]), .reset(Reset));  // open: Qn, preset
  Multiplexer multiplexer_13 (.in0(Dout[3]), .in1(Din[3]), .out(multiplexer_13_out), .sel(Write));
  D_Flip_Flop d_ff_14 (.D(multiplexer_14_out), .clk(Clk), .Q(Dout[11]), .reset(Reset));  // open: Qn, preset
  Multiplexer multiplexer_14 (.in0(Dout[11]), .in1(Din[11]), .out(multiplexer_14_out), .sel(Write));
  D_Flip_Flop d_ff_15 (.D(multiplexer_15_out), .clk(Clk), .Q(Dout[19]), .reset(Reset));  // open: Qn, preset
  Multiplexer multiplexer_15 (.in0(Dout[19]), .in1(Din[19]), .out(multiplexer_15_out), .sel(Write));
  D_Flip_Flop d_ff_16 (.D(multiplexer_16_out), .clk(Clk), .Q(Dout[27]), .reset(Reset));  // open: Qn, preset
  Multiplexer multiplexer_16 (.in0(Dout[27]), .in1(Din[27]), .out(multiplexer_16_out), .sel(Write));
  D_Flip_Flop d_ff_17 (.D(multiplexer_17_out), .clk(Clk), .Q(Dout[4]), .reset(Reset));  // open: Qn, preset
  Multiplexer multiplexer_17 (.in0(Dout[4]), .in1(Din[4]), .out(multiplexer_17_out), .sel(Write));
  D_Flip_Flop d_ff_18 (.D(multiplexer_18_out), .clk(Clk), .Q(Dout[12]), .reset(Reset));  // open: Qn, preset
  Multiplexer multiplexer_18 (.in0(Dout[12]), .in1(Din[12]), .out(multiplexer_18_out), .sel(Write));
  D_Flip_Flop d_ff_19 (.D(multiplexer_19_out), .clk(Clk), .Q(Dout[20]), .reset(Reset));  // open: Qn, preset
  Multiplexer multiplexer_19 (.in0(Dout[20]), .in1(Din[20]), .out(multiplexer_19_out), .sel(Write));
  D_Flip_Flop d_ff_20 (.D(multiplexer_20_out), .clk(Clk), .Q(Dout[28]), .reset(Reset));  // open: Qn, preset
  Multiplexer multiplexer_20 (.in0(Dout[28]), .in1(Din[28]), .out(multiplexer_20_out), .sel(Write));
  D_Flip_Flop d_ff_21 (.D(multiplexer_21_out), .clk(Clk), .Q(Dout[5]), .reset(Reset));  // open: Qn, preset
  Multiplexer multiplexer_21 (.in0(Dout[5]), .in1(Din[5]), .out(multiplexer_21_out), .sel(Write));
  D_Flip_Flop d_ff_22 (.D(multiplexer_22_out), .clk(Clk), .Q(Dout[13]), .reset(Reset));  // open: Qn, preset
  Multiplexer multiplexer_22 (.in0(Dout[13]), .in1(Din[13]), .out(multiplexer_22_out), .sel(Write));
  D_Flip_Flop d_ff_23 (.D(multiplexer_23_out), .clk(Clk), .Q(Dout[21]), .reset(Reset));  // open: Qn, preset
  Multiplexer multiplexer_23 (.in0(Dout[21]), .in1(Din[21]), .out(multiplexer_23_out), .sel(Write));
  D_Flip_Flop d_ff_24 (.D(multiplexer_24_out), .clk(Clk), .Q(Dout[29]), .reset(Reset));  // open: Qn, preset
  Multiplexer multiplexer_24 (.in0(Dout[29]), .in1(Din[29]), .out(multiplexer_24_out), .sel(Write));
  D_Flip_Flop d_ff_25 (.D(multiplexer_25_out), .clk(Clk), .Q(Dout[6]), .reset(Reset));  // open: Qn, preset
  Multiplexer multiplexer_25 (.in0(Dout[6]), .in1(Din[6]), .out(multiplexer_25_out), .sel(Write));
  D_Flip_Flop d_ff_26 (.D(multiplexer_26_out), .clk(Clk), .Q(Dout[14]), .reset(Reset));  // open: Qn, preset
  Multiplexer multiplexer_26 (.in0(Dout[14]), .in1(Din[14]), .out(multiplexer_26_out), .sel(Write));
  D_Flip_Flop d_ff_27 (.D(multiplexer_27_out), .clk(Clk), .Q(Dout[22]), .reset(Reset));  // open: Qn, preset
  Multiplexer multiplexer_27 (.in0(Dout[22]), .in1(Din[22]), .out(multiplexer_27_out), .sel(Write));
  D_Flip_Flop d_ff_28 (.D(multiplexer_28_out), .clk(Clk), .Q(Dout[30]), .reset(Reset));  // open: Qn, preset
  Multiplexer multiplexer_28 (.in0(Dout[30]), .in1(Din[30]), .out(multiplexer_28_out), .sel(Write));
  D_Flip_Flop d_ff_29 (.D(multiplexer_29_out), .clk(Clk), .Q(Dout[7]), .reset(Reset));  // open: Qn, preset
  Multiplexer multiplexer_29 (.in0(Dout[7]), .in1(Din[7]), .out(multiplexer_29_out), .sel(Write));
  D_Flip_Flop d_ff_30 (.D(multiplexer_30_out), .clk(Clk), .Q(Dout[15]), .reset(Reset));  // open: Qn, preset
  Multiplexer multiplexer_30 (.in0(Dout[15]), .in1(Din[15]), .out(multiplexer_30_out), .sel(Write));
  D_Flip_Flop d_ff_31 (.D(multiplexer_31_out), .clk(Clk), .Q(Dout[23]), .reset(Reset));  // open: Qn, preset
  Multiplexer multiplexer_31 (.in0(Dout[23]), .in1(Din[23]), .out(multiplexer_31_out), .sel(Write));
  D_Flip_Flop d_ff_32 (.D(multiplexer_32_out), .clk(Clk), .Q(Dout[31]), .reset(Reset));  // open: Qn, preset
  Multiplexer multiplexer_32 (.in0(Dout[31]), .in1(Din[31]), .out(multiplexer_32_out), .sel(Write));

  // Other names for the same wires on the sheet: C = Clk; R = Reset; W = Write
endmodule

module register_file_2x2_32 (
  input  WE_A,
  input  WE_B,
  input  [3:0] WAddr_A,
  input  [3:0] WAddr_B,
  input  [31:0] Din_A,
  input  [31:0] Din_B,
  input  [3:0] RAddr_A,
  input  [3:0] RAddr_B,
  input  Clk,
  output [31:0] Dout_A,
  output [31:0] Dout_B
);

  wire decoder_1_out0, decoder_1_out1, decoder_1_out2, decoder_1_out3, decoder_1_out4, decoder_1_out5,
       decoder_1_out6, decoder_1_out7, decoder_1_out8, decoder_1_out9, decoder_1_out10, decoder_1_out11,
       decoder_1_out12, decoder_1_out13, decoder_1_out14, decoder_1_out15, decoder_2_out0, decoder_2_out1,
       decoder_2_out2, decoder_2_out3, decoder_2_out4, decoder_2_out5, decoder_2_out6, decoder_2_out7,
       decoder_2_out8, decoder_2_out9, decoder_2_out10, decoder_2_out11, decoder_2_out12, decoder_2_out13,
       decoder_2_out14, decoder_2_out15, or_1_out, or_2_out, or_3_out, or_4_out, or_5_out, or_6_out,
       or_7_out, or_8_out, or_9_out, or_10_out, or_11_out, or_12_out, or_13_out, or_14_out, or_15_out,
       or_16_out;
  wire [31:0] mux2to1_32bit_1_out_4, mux2to1_32bit_2_out_4, mux2to1_32bit_3_out_4, mux2to1_32bit_4_out_4,
       mux2to1_32bit_5_out_4, mux2to1_32bit_6_out_4, mux2to1_32bit_7_out_4, mux2to1_32bit_8_out_4,
       mux2to1_32bit_9_out_4, mux2to1_32bit_10_out_4, mux2to1_32bit_11_out_4, mux2to1_32bit_12_out_4,
       mux2to1_32bit_13_out_4, mux2to1_32bit_14_out_4, mux2to1_32bit_15_out_4, mux2to1_32bit_16_out_4,
       register_32bit_1_dout, register_32bit_2_dout, register_32bit_3_dout, register_32bit_4_dout,
       register_32bit_5_dout, register_32bit_6_dout, register_32bit_7_dout, register_32bit_8_dout,
       register_32bit_9_dout, register_32bit_10_dout, register_32bit_11_dout, register_32bit_12_dout,
       register_32bit_13_dout, register_32bit_14_dout, register_32bit_15_dout, register_32bit_16_dout;

  // Probe on WE_A
  // Probe on WAddr_A
  Decoder #(.select(4)) decoder_1 (
    .out0(decoder_1_out0), .out1(decoder_1_out1), .out2(decoder_1_out2), .out3(decoder_1_out3),
    .out4(decoder_1_out4), .out5(decoder_1_out5), .out6(decoder_1_out6), .out7(decoder_1_out7),
    .out8(decoder_1_out8), .out9(decoder_1_out9), .out10(decoder_1_out10), .out11(decoder_1_out11),
    .out12(decoder_1_out12), .out13(decoder_1_out13), .out14(decoder_1_out14), .out15(decoder_1_out15),
    .sel(WAddr_A), .en(WE_A));
  Decoder #(.select(4)) decoder_2 (
    .out0(decoder_2_out0), .out1(decoder_2_out1), .out2(decoder_2_out2), .out3(decoder_2_out3),
    .out4(decoder_2_out4), .out5(decoder_2_out5), .out6(decoder_2_out6), .out7(decoder_2_out7),
    .out8(decoder_2_out8), .out9(decoder_2_out9), .out10(decoder_2_out10), .out11(decoder_2_out11),
    .out12(decoder_2_out12), .out13(decoder_2_out13), .out14(decoder_2_out14), .out15(decoder_2_out15),
    .sel(WAddr_B), .en(WE_B));
  or or_1 (or_1_out, decoder_1_out0, decoder_2_out0);
  or or_2 (or_2_out, decoder_1_out1, decoder_2_out1);
  or or_3 (or_3_out, decoder_1_out2, decoder_2_out2);
  or or_4 (or_4_out, decoder_1_out3, decoder_2_out3);
  or or_5 (or_5_out, decoder_1_out4, decoder_2_out4);
  or or_6 (or_6_out, decoder_1_out5, decoder_2_out5);
  or or_7 (or_7_out, decoder_1_out6, decoder_2_out6);
  or or_8 (or_8_out, decoder_1_out7, decoder_2_out7);
  or or_9 (or_9_out, decoder_1_out8, decoder_2_out8);
  or or_10 (or_10_out, decoder_1_out9, decoder_2_out9);
  or or_11 (or_11_out, decoder_1_out10, decoder_2_out10);
  or or_12 (or_12_out, decoder_1_out11, decoder_2_out11);
  or or_13 (or_13_out, decoder_1_out12, decoder_2_out12);
  or or_14 (or_14_out, decoder_1_out13, decoder_2_out13);
  or or_15 (or_15_out, decoder_1_out14, decoder_2_out14);
  or or_16 (or_16_out, decoder_1_out15, decoder_2_out15);
  MUX2to1_32bit mux2to1_32bit_1 (.A(Din_A), .B(Din_B), .in_3(decoder_2_out0), .out_4(mux2to1_32bit_1_out_4));
  MUX2to1_32bit mux2to1_32bit_2 (.A(Din_A), .B(Din_B), .in_3(decoder_2_out1), .out_4(mux2to1_32bit_2_out_4));
  MUX2to1_32bit mux2to1_32bit_3 (.A(Din_A), .B(Din_B), .in_3(decoder_2_out2), .out_4(mux2to1_32bit_3_out_4));
  MUX2to1_32bit mux2to1_32bit_4 (.A(Din_A), .B(Din_B), .in_3(decoder_2_out3), .out_4(mux2to1_32bit_4_out_4));
  MUX2to1_32bit mux2to1_32bit_5 (.A(Din_A), .B(Din_B), .in_3(decoder_2_out4), .out_4(mux2to1_32bit_5_out_4));
  MUX2to1_32bit mux2to1_32bit_6 (.A(Din_A), .B(Din_B), .in_3(decoder_2_out5), .out_4(mux2to1_32bit_6_out_4));
  MUX2to1_32bit mux2to1_32bit_7 (.A(Din_A), .B(Din_B), .in_3(decoder_2_out6), .out_4(mux2to1_32bit_7_out_4));
  MUX2to1_32bit mux2to1_32bit_8 (.A(Din_A), .B(Din_B), .in_3(decoder_2_out7), .out_4(mux2to1_32bit_8_out_4));
  MUX2to1_32bit mux2to1_32bit_9 (.A(Din_A), .B(Din_B), .in_3(decoder_2_out8), .out_4(mux2to1_32bit_9_out_4));
  MUX2to1_32bit mux2to1_32bit_10 (.A(Din_A), .B(Din_B), .in_3(decoder_2_out9), .out_4(mux2to1_32bit_10_out_4));
  MUX2to1_32bit mux2to1_32bit_11 (.A(Din_A), .B(Din_B), .in_3(decoder_2_out10), .out_4(mux2to1_32bit_11_out_4));
  MUX2to1_32bit mux2to1_32bit_12 (.A(Din_A), .B(Din_B), .in_3(decoder_2_out11), .out_4(mux2to1_32bit_12_out_4));
  MUX2to1_32bit mux2to1_32bit_13 (.A(Din_A), .B(Din_B), .in_3(decoder_2_out12), .out_4(mux2to1_32bit_13_out_4));
  MUX2to1_32bit mux2to1_32bit_14 (.A(Din_A), .B(Din_B), .in_3(decoder_2_out13), .out_4(mux2to1_32bit_14_out_4));
  MUX2to1_32bit mux2to1_32bit_15 (.A(Din_A), .B(Din_B), .in_3(decoder_2_out14), .out_4(mux2to1_32bit_15_out_4));
  MUX2to1_32bit mux2to1_32bit_16 (.A(Din_A), .B(Din_B), .in_3(decoder_2_out15), .out_4(mux2to1_32bit_16_out_4));
  Register_32bit register_32bit_1 (
    .Din(mux2to1_32bit_1_out_4), .Write(or_1_out), .Clk(Clk), .Dout(register_32bit_1_dout));  // open: Reset
  Register_32bit register_32bit_2 (
    .Din(mux2to1_32bit_2_out_4), .Write(or_2_out), .Clk(Clk), .Dout(register_32bit_2_dout));  // open: Reset
  Register_32bit register_32bit_3 (
    .Din(mux2to1_32bit_3_out_4), .Write(or_3_out), .Clk(Clk), .Dout(register_32bit_3_dout));  // open: Reset
  Register_32bit register_32bit_4 (
    .Din(mux2to1_32bit_4_out_4), .Write(or_4_out), .Clk(Clk), .Dout(register_32bit_4_dout));  // open: Reset
  Register_32bit register_32bit_5 (
    .Din(mux2to1_32bit_5_out_4), .Write(or_5_out), .Clk(Clk), .Dout(register_32bit_5_dout));  // open: Reset
  Register_32bit register_32bit_6 (
    .Din(mux2to1_32bit_6_out_4), .Write(or_6_out), .Clk(Clk), .Dout(register_32bit_6_dout));  // open: Reset
  Register_32bit register_32bit_7 (
    .Din(mux2to1_32bit_7_out_4), .Write(or_7_out), .Clk(Clk), .Dout(register_32bit_7_dout));  // open: Reset
  Register_32bit register_32bit_8 (
    .Din(mux2to1_32bit_8_out_4), .Write(or_8_out), .Clk(Clk), .Dout(register_32bit_8_dout));  // open: Reset
  Register_32bit register_32bit_9 (
    .Din(mux2to1_32bit_9_out_4), .Write(or_9_out), .Clk(Clk), .Dout(register_32bit_9_dout));  // open: Reset
  Register_32bit register_32bit_10 (
    .Din(mux2to1_32bit_10_out_4), .Write(or_10_out), .Clk(Clk), .Dout(register_32bit_10_dout));  // open: Reset
  Register_32bit register_32bit_11 (
    .Din(mux2to1_32bit_11_out_4), .Write(or_11_out), .Clk(Clk), .Dout(register_32bit_11_dout));  // open: Reset
  Register_32bit register_32bit_12 (
    .Din(mux2to1_32bit_12_out_4), .Write(or_12_out), .Clk(Clk), .Dout(register_32bit_12_dout));  // open: Reset
  Register_32bit register_32bit_13 (
    .Din(mux2to1_32bit_13_out_4), .Write(or_13_out), .Clk(Clk), .Dout(register_32bit_13_dout));  // open: Reset
  Register_32bit register_32bit_14 (
    .Din(mux2to1_32bit_14_out_4), .Write(or_14_out), .Clk(Clk), .Dout(register_32bit_14_dout));  // open: Reset
  Register_32bit register_32bit_15 (
    .Din(mux2to1_32bit_15_out_4), .Write(or_15_out), .Clk(Clk), .Dout(register_32bit_15_dout));  // open: Reset
  Register_32bit register_32bit_16 (
    .Din(mux2to1_32bit_16_out_4), .Write(or_16_out), .Clk(Clk), .Dout(register_32bit_16_dout));  // open: Reset
  Multiplexer #(.select(4), .width(32)) multiplexer_1 (
    .in0(register_32bit_1_dout), .in1(register_32bit_2_dout), .in2(register_32bit_3_dout),
    .in3(register_32bit_4_dout), .in4(register_32bit_5_dout), .in5(register_32bit_6_dout),
    .in6(register_32bit_7_dout), .in7(register_32bit_8_dout), .in8(register_32bit_9_dout),
    .in9(register_32bit_10_dout), .in10(register_32bit_11_dout), .in11(register_32bit_12_dout),
    .in12(register_32bit_13_dout), .in13(register_32bit_14_dout), .in14(register_32bit_15_dout),
    .in15(register_32bit_16_dout), .out(Dout_A), .sel(RAddr_A));
  Multiplexer #(.select(4), .width(32)) multiplexer_2 (
    .in0(register_32bit_1_dout), .in1(register_32bit_2_dout), .in2(register_32bit_3_dout),
    .in3(register_32bit_4_dout), .in4(register_32bit_5_dout), .in5(register_32bit_6_dout),
    .in6(register_32bit_7_dout), .in7(register_32bit_8_dout), .in8(register_32bit_9_dout),
    .in9(register_32bit_10_dout), .in10(register_32bit_11_dout), .in11(register_32bit_12_dout),
    .in12(register_32bit_13_dout), .in13(register_32bit_14_dout), .in14(register_32bit_15_dout),
    .in15(register_32bit_16_dout), .out(Dout_B), .sel(RAddr_B));

  // Other names for the same wires on the sheet: A_RA[3:0] = RAddr_A; A_WA[3:0] = WAddr_A; A_WE = WE_A;
  //   B_RA[3:0] = RAddr_B; B_WA[3:0] = WAddr_B; B_WE = WE_B; C = Clk; IN_A[31:0] = Din_A; IN_B[31:0] = Din_B
endmodule

module register_3bit (
  input  [2:0] Din,
  input  Write,
  input  Clk,
  output [2:0] Dout
);

  wire multiplexer_1_out, multiplexer_2_out, multiplexer_3_out;

  D_Flip_Flop d_ff_1 (.D(multiplexer_1_out), .clk(Clk), .Q(Dout[0]));  // open: Qn, preset, reset
  Multiplexer multiplexer_1 (.in0(Dout[0]), .in1(Din[0]), .out(multiplexer_1_out), .sel(Write));
  D_Flip_Flop d_ff_2 (.D(multiplexer_2_out), .clk(Clk), .Q(Dout[1]));  // open: Qn, preset, reset
  Multiplexer multiplexer_2 (.in0(Dout[1]), .in1(Din[1]), .out(multiplexer_2_out), .sel(Write));
  D_Flip_Flop d_ff_3 (.D(multiplexer_3_out), .clk(Clk), .Q(Dout[2]));  // open: Qn, preset, reset
  Multiplexer multiplexer_3 (.in0(Dout[2]), .in1(Din[2]), .out(multiplexer_3_out), .sel(Write));
endmodule

module register_file_3bit (
  input  WE,
  input  [2:0] WAddr,
  input  [2:0] Data_in,
  input  Clk,
  input  [2:0] RAddr,
  output [2:0] Data_out
);

  wire decoder_1_out0, decoder_1_out1, decoder_1_out2, decoder_1_out3, decoder_1_out4, decoder_1_out5,
       decoder_1_out6, decoder_1_out7;
  wire [2:0] register_3bit_1_dout, register_3bit_2_dout, register_3bit_3_dout, register_3bit_4_dout,
       register_3bit_5_dout, register_3bit_6_dout, register_3bit_7_dout, register_3bit_8_dout;

  Decoder #(.select(3)) decoder_1 (
    .out0(decoder_1_out0), .out1(decoder_1_out1), .out2(decoder_1_out2), .out3(decoder_1_out3),
    .out4(decoder_1_out4), .out5(decoder_1_out5), .out6(decoder_1_out6), .out7(decoder_1_out7), .sel(WAddr),
    .en(WE));
  register_3bit register_3bit_1 (.Din(Data_in), .Write(decoder_1_out0), .Clk(Clk), .Dout(register_3bit_1_dout));
  register_3bit register_3bit_2 (.Din(Data_in), .Write(decoder_1_out1), .Clk(Clk), .Dout(register_3bit_2_dout));
  register_3bit register_3bit_3 (.Din(Data_in), .Write(decoder_1_out2), .Clk(Clk), .Dout(register_3bit_3_dout));
  register_3bit register_3bit_4 (.Din(Data_in), .Write(decoder_1_out3), .Clk(Clk), .Dout(register_3bit_4_dout));
  register_3bit register_3bit_5 (.Din(Data_in), .Write(decoder_1_out4), .Clk(Clk), .Dout(register_3bit_5_dout));
  register_3bit register_3bit_6 (.Din(Data_in), .Write(decoder_1_out5), .Clk(Clk), .Dout(register_3bit_6_dout));
  register_3bit register_3bit_7 (.Din(Data_in), .Write(decoder_1_out6), .Clk(Clk), .Dout(register_3bit_7_dout));
  register_3bit register_3bit_8 (.Din(Data_in), .Write(decoder_1_out7), .Clk(Clk), .Dout(register_3bit_8_dout));
  Multiplexer #(.select(3), .width(3)) multiplexer_1 (
    .in0(register_3bit_1_dout), .in1(register_3bit_2_dout), .in2(register_3bit_3_dout),
    .in3(register_3bit_4_dout), .in4(register_3bit_5_dout), .in5(register_3bit_6_dout),
    .in6(register_3bit_7_dout), .in7(register_3bit_8_dout), .out(Data_out), .sel(RAddr));
endmodule

module V_LSR_32bit (
  input  [31:0] in_1,
  input  [4:0] Shift,
  output [31:0] out_3
);

  wire multiplexer_1_out, multiplexer_2_out, multiplexer_3_out, multiplexer_4_out, multiplexer_5_out,
       multiplexer_6_out, multiplexer_7_out, multiplexer_8_out, multiplexer_9_out, multiplexer_10_out,
       multiplexer_11_out, multiplexer_12_out, multiplexer_13_out, multiplexer_14_out, multiplexer_15_out,
       multiplexer_16_out, multiplexer_17_out, multiplexer_18_out, multiplexer_19_out, multiplexer_20_out,
       multiplexer_21_out, multiplexer_22_out, multiplexer_23_out, multiplexer_24_out, multiplexer_25_out,
       multiplexer_26_out, multiplexer_27_out, multiplexer_28_out, multiplexer_29_out, multiplexer_30_out,
       multiplexer_31_out, multiplexer_32_out, multiplexer_33_out, multiplexer_34_out, multiplexer_35_out,
       multiplexer_36_out, multiplexer_37_out, multiplexer_38_out, multiplexer_39_out, multiplexer_40_out,
       multiplexer_41_out, multiplexer_42_out, multiplexer_43_out, multiplexer_44_out, multiplexer_45_out,
       multiplexer_46_out, multiplexer_47_out, multiplexer_48_out, multiplexer_49_out, multiplexer_50_out,
       multiplexer_51_out, multiplexer_52_out, multiplexer_53_out, multiplexer_54_out, multiplexer_55_out,
       multiplexer_56_out, multiplexer_57_out, multiplexer_58_out, multiplexer_59_out, multiplexer_60_out,
       multiplexer_61_out, multiplexer_62_out, multiplexer_63_out, multiplexer_64_out, multiplexer_65_out,
       multiplexer_66_out, multiplexer_67_out, multiplexer_68_out, multiplexer_69_out, multiplexer_70_out,
       multiplexer_71_out, multiplexer_72_out, multiplexer_73_out, multiplexer_74_out, multiplexer_75_out,
       multiplexer_76_out, multiplexer_77_out, multiplexer_78_out, multiplexer_79_out, multiplexer_80_out,
       multiplexer_81_out, multiplexer_82_out, multiplexer_83_out, multiplexer_84_out, multiplexer_85_out,
       multiplexer_86_out, multiplexer_87_out, multiplexer_88_out, multiplexer_89_out, multiplexer_90_out,
       multiplexer_91_out, multiplexer_92_out, multiplexer_93_out, multiplexer_94_out, multiplexer_95_out,
       multiplexer_96_out, multiplexer_97_out, multiplexer_98_out, multiplexer_99_out, multiplexer_100_out,
       multiplexer_101_out, multiplexer_102_out, multiplexer_103_out, multiplexer_104_out,
       multiplexer_105_out, multiplexer_106_out, multiplexer_107_out, multiplexer_108_out,
       multiplexer_109_out, multiplexer_110_out, multiplexer_111_out, multiplexer_112_out,
       multiplexer_113_out, multiplexer_114_out, multiplexer_115_out, multiplexer_116_out,
       multiplexer_117_out, multiplexer_118_out, multiplexer_119_out, multiplexer_120_out,
       multiplexer_121_out, multiplexer_122_out, multiplexer_123_out, multiplexer_124_out,
       multiplexer_125_out, multiplexer_126_out, multiplexer_127_out, multiplexer_128_out;

  Multiplexer multiplexer_1 (.in0(in_1[0]), .in1(in_1[1]), .out(multiplexer_1_out), .sel(Shift[0]));
  Multiplexer multiplexer_2 (.in0(in_1[2]), .in1(in_1[3]), .out(multiplexer_2_out), .sel(Shift[0]));
  Multiplexer multiplexer_3 (.in0(in_1[4]), .in1(in_1[5]), .out(multiplexer_3_out), .sel(Shift[0]));
  Multiplexer multiplexer_4 (.in0(in_1[6]), .in1(in_1[7]), .out(multiplexer_4_out), .sel(Shift[0]));
  Multiplexer multiplexer_5 (.in0(in_1[8]), .in1(in_1[9]), .out(multiplexer_5_out), .sel(Shift[0]));
  Multiplexer multiplexer_6 (.in0(in_1[10]), .in1(in_1[11]), .out(multiplexer_6_out), .sel(Shift[0]));
  Multiplexer multiplexer_7 (.in0(in_1[12]), .in1(in_1[13]), .out(multiplexer_7_out), .sel(Shift[0]));
  Multiplexer multiplexer_8 (.in0(in_1[14]), .in1(in_1[15]), .out(multiplexer_8_out), .sel(Shift[0]));
  Multiplexer multiplexer_9 (.in0(in_1[16]), .in1(in_1[17]), .out(multiplexer_9_out), .sel(Shift[0]));
  Multiplexer multiplexer_10 (.in0(in_1[18]), .in1(in_1[19]), .out(multiplexer_10_out), .sel(Shift[0]));
  Multiplexer multiplexer_11 (.in0(in_1[20]), .in1(in_1[21]), .out(multiplexer_11_out), .sel(Shift[0]));
  Multiplexer multiplexer_12 (.in0(in_1[22]), .in1(in_1[23]), .out(multiplexer_12_out), .sel(Shift[0]));
  Multiplexer multiplexer_13 (.in0(in_1[24]), .in1(in_1[25]), .out(multiplexer_13_out), .sel(Shift[0]));
  Multiplexer multiplexer_14 (.in0(in_1[26]), .in1(in_1[27]), .out(multiplexer_14_out), .sel(Shift[0]));
  Multiplexer multiplexer_15 (.in0(in_1[28]), .in1(in_1[29]), .out(multiplexer_15_out), .sel(Shift[0]));
  Multiplexer multiplexer_16 (.in0(in_1[30]), .in1(in_1[31]), .out(multiplexer_16_out), .sel(Shift[0]));
  Multiplexer multiplexer_17 (.in0(in_1[1]), .in1(in_1[2]), .out(multiplexer_17_out), .sel(Shift[0]));
  Multiplexer multiplexer_18 (.in0(in_1[3]), .in1(in_1[4]), .out(multiplexer_18_out), .sel(Shift[0]));
  Multiplexer multiplexer_19 (.in0(in_1[5]), .in1(in_1[6]), .out(multiplexer_19_out), .sel(Shift[0]));
  Multiplexer multiplexer_20 (.in0(in_1[7]), .in1(in_1[8]), .out(multiplexer_20_out), .sel(Shift[0]));
  Multiplexer multiplexer_21 (.in0(in_1[9]), .in1(in_1[10]), .out(multiplexer_21_out), .sel(Shift[0]));
  Multiplexer multiplexer_22 (.in0(in_1[11]), .in1(in_1[12]), .out(multiplexer_22_out), .sel(Shift[0]));
  Multiplexer multiplexer_23 (.in0(in_1[13]), .in1(in_1[14]), .out(multiplexer_23_out), .sel(Shift[0]));
  Multiplexer multiplexer_24 (.in0(in_1[15]), .in1(in_1[16]), .out(multiplexer_24_out), .sel(Shift[0]));
  Multiplexer multiplexer_25 (.in0(in_1[17]), .in1(in_1[18]), .out(multiplexer_25_out), .sel(Shift[0]));
  Multiplexer multiplexer_26 (.in0(in_1[19]), .in1(in_1[20]), .out(multiplexer_26_out), .sel(Shift[0]));
  Multiplexer multiplexer_27 (.in0(in_1[21]), .in1(in_1[22]), .out(multiplexer_27_out), .sel(Shift[0]));
  Multiplexer multiplexer_28 (.in0(in_1[23]), .in1(in_1[24]), .out(multiplexer_28_out), .sel(Shift[0]));
  Multiplexer multiplexer_29 (.in0(in_1[25]), .in1(in_1[26]), .out(multiplexer_29_out), .sel(Shift[0]));
  Multiplexer multiplexer_30 (.in0(in_1[27]), .in1(in_1[28]), .out(multiplexer_30_out), .sel(Shift[0]));
  Multiplexer multiplexer_31 (.in0(in_1[29]), .in1(in_1[30]), .out(multiplexer_31_out), .sel(Shift[0]));
  Multiplexer multiplexer_32 (.in0(in_1[31]), .in1(1'b0), .out(multiplexer_32_out), .sel(Shift[0]));
  Multiplexer multiplexer_33 (
    .in0(multiplexer_1_out), .in1(multiplexer_2_out), .out(multiplexer_33_out), .sel(Shift[1]));
  Multiplexer multiplexer_34 (
    .in0(multiplexer_2_out), .in1(multiplexer_3_out), .out(multiplexer_34_out), .sel(Shift[1]));
  Multiplexer multiplexer_35 (
    .in0(multiplexer_3_out), .in1(multiplexer_4_out), .out(multiplexer_35_out), .sel(Shift[1]));
  Multiplexer multiplexer_36 (
    .in0(multiplexer_4_out), .in1(multiplexer_5_out), .out(multiplexer_36_out), .sel(Shift[1]));
  Multiplexer multiplexer_37 (
    .in0(multiplexer_5_out), .in1(multiplexer_7_out), .out(multiplexer_37_out), .sel(Shift[1]));
  Multiplexer multiplexer_38 (
    .in0(multiplexer_6_out), .in1(multiplexer_7_out), .out(multiplexer_38_out), .sel(Shift[1]));
  Multiplexer multiplexer_39 (
    .in0(multiplexer_7_out), .in1(multiplexer_8_out), .out(multiplexer_39_out), .sel(Shift[1]));
  Multiplexer multiplexer_40 (
    .in0(multiplexer_8_out), .in1(multiplexer_9_out), .out(multiplexer_40_out), .sel(Shift[1]));
  Multiplexer multiplexer_41 (
    .in0(multiplexer_9_out), .in1(multiplexer_10_out), .out(multiplexer_41_out), .sel(Shift[1]));
  Multiplexer multiplexer_42 (
    .in0(multiplexer_10_out), .in1(multiplexer_11_out), .out(multiplexer_42_out), .sel(Shift[1]));
  Multiplexer multiplexer_43 (
    .in0(multiplexer_11_out), .in1(multiplexer_12_out), .out(multiplexer_43_out), .sel(Shift[1]));
  Multiplexer multiplexer_44 (
    .in0(multiplexer_12_out), .in1(multiplexer_13_out), .out(multiplexer_44_out), .sel(Shift[1]));
  Multiplexer multiplexer_45 (
    .in0(multiplexer_13_out), .in1(multiplexer_14_out), .out(multiplexer_45_out), .sel(Shift[1]));
  Multiplexer multiplexer_46 (
    .in0(multiplexer_14_out), .in1(multiplexer_15_out), .out(multiplexer_46_out), .sel(Shift[1]));
  Multiplexer multiplexer_47 (
    .in0(multiplexer_15_out), .in1(multiplexer_16_out), .out(multiplexer_47_out), .sel(Shift[1]));
  Multiplexer multiplexer_48 (.in0(multiplexer_16_out), .in1(1'b0), .out(multiplexer_48_out), .sel(Shift[1]));
  Multiplexer multiplexer_49 (
    .in0(multiplexer_17_out), .in1(multiplexer_18_out), .out(multiplexer_49_out), .sel(Shift[1]));
  Multiplexer multiplexer_50 (
    .in0(multiplexer_18_out), .in1(multiplexer_19_out), .out(multiplexer_50_out), .sel(Shift[1]));
  Multiplexer multiplexer_51 (
    .in0(multiplexer_19_out), .in1(multiplexer_20_out), .out(multiplexer_51_out), .sel(Shift[1]));
  Multiplexer multiplexer_52 (
    .in0(multiplexer_20_out), .in1(multiplexer_21_out), .out(multiplexer_52_out), .sel(Shift[1]));
  Multiplexer multiplexer_53 (
    .in0(multiplexer_21_out), .in1(multiplexer_22_out), .out(multiplexer_53_out), .sel(Shift[1]));
  Multiplexer multiplexer_54 (
    .in0(multiplexer_22_out), .in1(multiplexer_23_out), .out(multiplexer_54_out), .sel(Shift[1]));
  Multiplexer multiplexer_55 (
    .in0(multiplexer_23_out), .in1(multiplexer_24_out), .out(multiplexer_55_out), .sel(Shift[1]));
  Multiplexer multiplexer_56 (
    .in0(multiplexer_24_out), .in1(multiplexer_25_out), .out(multiplexer_56_out), .sel(Shift[1]));
  Multiplexer multiplexer_57 (
    .in0(multiplexer_25_out), .in1(multiplexer_26_out), .out(multiplexer_57_out), .sel(Shift[1]));
  Multiplexer multiplexer_58 (
    .in0(multiplexer_26_out), .in1(multiplexer_27_out), .out(multiplexer_58_out), .sel(Shift[1]));
  Multiplexer multiplexer_59 (
    .in0(multiplexer_27_out), .in1(multiplexer_28_out), .out(multiplexer_59_out), .sel(Shift[1]));
  Multiplexer multiplexer_60 (
    .in0(multiplexer_28_out), .in1(multiplexer_29_out), .out(multiplexer_60_out), .sel(Shift[1]));
  Multiplexer multiplexer_61 (
    .in0(multiplexer_29_out), .in1(multiplexer_30_out), .out(multiplexer_61_out), .sel(Shift[1]));
  Multiplexer multiplexer_62 (
    .in0(multiplexer_30_out), .in1(multiplexer_31_out), .out(multiplexer_62_out), .sel(Shift[1]));
  Multiplexer multiplexer_63 (
    .in0(multiplexer_31_out), .in1(multiplexer_32_out), .out(multiplexer_63_out), .sel(Shift[1]));
  Multiplexer multiplexer_64 (.in0(multiplexer_32_out), .in1(1'b0), .out(multiplexer_64_out), .sel(Shift[1]));
  Multiplexer multiplexer_65 (
    .in0(multiplexer_33_out), .in1(multiplexer_35_out), .out(multiplexer_65_out), .sel(Shift[2]));
  Multiplexer multiplexer_66 (
    .in0(multiplexer_49_out), .in1(multiplexer_51_out), .out(multiplexer_66_out), .sel(Shift[2]));
  Multiplexer multiplexer_67 (
    .in0(multiplexer_34_out), .in1(multiplexer_36_out), .out(multiplexer_67_out), .sel(Shift[2]));
  Multiplexer multiplexer_68 (
    .in0(multiplexer_50_out), .in1(multiplexer_52_out), .out(multiplexer_68_out), .sel(Shift[2]));
  Multiplexer multiplexer_69 (
    .in0(multiplexer_35_out), .in1(multiplexer_37_out), .out(multiplexer_69_out), .sel(Shift[2]));
  Multiplexer multiplexer_70 (
    .in0(multiplexer_51_out), .in1(multiplexer_53_out), .out(multiplexer_70_out), .sel(Shift[2]));
  Multiplexer multiplexer_71 (
    .in0(multiplexer_36_out), .in1(multiplexer_38_out), .out(multiplexer_71_out), .sel(Shift[2]));
  Multiplexer multiplexer_72 (
    .in0(multiplexer_52_out), .in1(multiplexer_54_out), .out(multiplexer_72_out), .sel(Shift[2]));
  Multiplexer multiplexer_73 (
    .in0(multiplexer_37_out), .in1(multiplexer_39_out), .out(multiplexer_73_out), .sel(Shift[2]));
  Multiplexer multiplexer_74 (
    .in0(multiplexer_53_out), .in1(multiplexer_55_out), .out(multiplexer_74_out), .sel(Shift[2]));
  Multiplexer multiplexer_75 (
    .in0(multiplexer_38_out), .in1(multiplexer_40_out), .out(multiplexer_75_out), .sel(Shift[2]));
  Multiplexer multiplexer_76 (
    .in0(multiplexer_54_out), .in1(multiplexer_56_out), .out(multiplexer_76_out), .sel(Shift[2]));
  Multiplexer multiplexer_77 (
    .in0(multiplexer_39_out), .in1(multiplexer_41_out), .out(multiplexer_77_out), .sel(Shift[2]));
  Multiplexer multiplexer_78 (
    .in0(multiplexer_55_out), .in1(multiplexer_57_out), .out(multiplexer_78_out), .sel(Shift[2]));
  Multiplexer multiplexer_79 (
    .in0(multiplexer_40_out), .in1(multiplexer_42_out), .out(multiplexer_79_out), .sel(Shift[2]));
  Multiplexer multiplexer_80 (
    .in0(multiplexer_56_out), .in1(multiplexer_58_out), .out(multiplexer_80_out), .sel(Shift[2]));
  Multiplexer multiplexer_81 (
    .in0(multiplexer_41_out), .in1(multiplexer_43_out), .out(multiplexer_81_out), .sel(Shift[2]));
  Multiplexer multiplexer_82 (
    .in0(multiplexer_57_out), .in1(multiplexer_59_out), .out(multiplexer_82_out), .sel(Shift[2]));
  Multiplexer multiplexer_83 (
    .in0(multiplexer_42_out), .in1(multiplexer_44_out), .out(multiplexer_83_out), .sel(Shift[2]));
  Multiplexer multiplexer_84 (
    .in0(multiplexer_58_out), .in1(multiplexer_60_out), .out(multiplexer_84_out), .sel(Shift[2]));
  Multiplexer multiplexer_85 (
    .in0(multiplexer_43_out), .in1(multiplexer_45_out), .out(multiplexer_85_out), .sel(Shift[2]));
  Multiplexer multiplexer_86 (
    .in0(multiplexer_59_out), .in1(multiplexer_61_out), .out(multiplexer_86_out), .sel(Shift[2]));
  Multiplexer multiplexer_87 (
    .in0(multiplexer_44_out), .in1(multiplexer_46_out), .out(multiplexer_87_out), .sel(Shift[2]));
  Multiplexer multiplexer_88 (
    .in0(multiplexer_60_out), .in1(multiplexer_62_out), .out(multiplexer_88_out), .sel(Shift[2]));
  Multiplexer multiplexer_89 (
    .in0(multiplexer_45_out), .in1(multiplexer_47_out), .out(multiplexer_89_out), .sel(Shift[2]));
  Multiplexer multiplexer_90 (
    .in0(multiplexer_61_out), .in1(multiplexer_63_out), .out(multiplexer_90_out), .sel(Shift[2]));
  Multiplexer multiplexer_91 (
    .in0(multiplexer_46_out), .in1(multiplexer_48_out), .out(multiplexer_91_out), .sel(Shift[2]));
  Multiplexer multiplexer_92 (
    .in0(multiplexer_62_out), .in1(multiplexer_64_out), .out(multiplexer_92_out), .sel(Shift[2]));
  Multiplexer multiplexer_93 (.in0(multiplexer_47_out), .in1(1'b0), .out(multiplexer_93_out), .sel(Shift[2]));
  Multiplexer multiplexer_94 (.in0(multiplexer_63_out), .in1(1'b0), .out(multiplexer_94_out), .sel(Shift[2]));
  Multiplexer multiplexer_95 (.in0(multiplexer_48_out), .in1(1'b0), .out(multiplexer_95_out), .sel(Shift[2]));
  Multiplexer multiplexer_96 (.in0(multiplexer_64_out), .in1(1'b0), .out(multiplexer_96_out), .sel(Shift[2]));
  Multiplexer multiplexer_97 (
    .in0(multiplexer_65_out), .in1(multiplexer_73_out), .out(multiplexer_97_out), .sel(Shift[3]));
  Multiplexer multiplexer_98 (
    .in0(multiplexer_67_out), .in1(multiplexer_75_out), .out(multiplexer_98_out), .sel(Shift[3]));
  Multiplexer multiplexer_99 (
    .in0(multiplexer_69_out), .in1(multiplexer_77_out), .out(multiplexer_99_out), .sel(Shift[3]));
  Multiplexer multiplexer_100 (
    .in0(multiplexer_71_out), .in1(multiplexer_79_out), .out(multiplexer_100_out), .sel(Shift[3]));
  Multiplexer multiplexer_101 (
    .in0(multiplexer_73_out), .in1(multiplexer_81_out), .out(multiplexer_101_out), .sel(Shift[3]));
  Multiplexer multiplexer_102 (
    .in0(multiplexer_75_out), .in1(multiplexer_83_out), .out(multiplexer_102_out), .sel(Shift[3]));
  Multiplexer multiplexer_103 (
    .in0(multiplexer_77_out), .in1(multiplexer_85_out), .out(multiplexer_103_out), .sel(Shift[3]));
  Multiplexer multiplexer_104 (
    .in0(multiplexer_79_out), .in1(multiplexer_87_out), .out(multiplexer_104_out), .sel(Shift[3]));
  Multiplexer multiplexer_105 (
    .in0(multiplexer_81_out), .in1(multiplexer_89_out), .out(multiplexer_105_out), .sel(Shift[3]));
  Multiplexer multiplexer_106 (
    .in0(multiplexer_83_out), .in1(multiplexer_91_out), .out(multiplexer_106_out), .sel(Shift[3]));
  Multiplexer multiplexer_107 (
    .in0(multiplexer_85_out), .in1(multiplexer_93_out), .out(multiplexer_107_out), .sel(Shift[3]));
  Multiplexer multiplexer_108 (
    .in0(multiplexer_87_out), .in1(multiplexer_95_out), .out(multiplexer_108_out), .sel(Shift[3]));
  Multiplexer multiplexer_109 (.in0(multiplexer_89_out), .in1(1'b0), .out(multiplexer_109_out), .sel(Shift[3]));
  Multiplexer multiplexer_110 (.in0(multiplexer_91_out), .in1(1'b0), .out(multiplexer_110_out), .sel(Shift[3]));
  Multiplexer multiplexer_111 (.in0(multiplexer_93_out), .in1(1'b0), .out(multiplexer_111_out), .sel(Shift[3]));
  Multiplexer multiplexer_112 (.in0(multiplexer_95_out), .in1(1'b0), .out(multiplexer_112_out), .sel(Shift[3]));
  Multiplexer multiplexer_113 (
    .in0(multiplexer_66_out), .in1(multiplexer_74_out), .out(multiplexer_113_out), .sel(Shift[3]));
  Multiplexer multiplexer_114 (
    .in0(multiplexer_68_out), .in1(multiplexer_76_out), .out(multiplexer_114_out), .sel(Shift[3]));
  Multiplexer multiplexer_115 (
    .in0(multiplexer_70_out), .in1(multiplexer_78_out), .out(multiplexer_115_out), .sel(Shift[3]));
  Multiplexer multiplexer_116 (
    .in0(multiplexer_72_out), .in1(multiplexer_80_out), .out(multiplexer_116_out), .sel(Shift[3]));
  Multiplexer multiplexer_117 (
    .in0(multiplexer_74_out), .in1(multiplexer_82_out), .out(multiplexer_117_out), .sel(Shift[3]));
  Multiplexer multiplexer_118 (
    .in0(multiplexer_76_out), .in1(multiplexer_84_out), .out(multiplexer_118_out), .sel(Shift[3]));
  Multiplexer multiplexer_119 (
    .in0(multiplexer_78_out), .in1(multiplexer_86_out), .out(multiplexer_119_out), .sel(Shift[3]));
  Multiplexer multiplexer_120 (
    .in0(multiplexer_80_out), .in1(multiplexer_88_out), .out(multiplexer_120_out), .sel(Shift[3]));
  Multiplexer multiplexer_121 (
    .in0(multiplexer_82_out), .in1(multiplexer_90_out), .out(multiplexer_121_out), .sel(Shift[3]));
  Multiplexer multiplexer_122 (
    .in0(multiplexer_84_out), .in1(multiplexer_92_out), .out(multiplexer_122_out), .sel(Shift[3]));
  Multiplexer multiplexer_123 (
    .in0(multiplexer_86_out), .in1(multiplexer_94_out), .out(multiplexer_123_out), .sel(Shift[3]));
  Multiplexer multiplexer_124 (
    .in0(multiplexer_88_out), .in1(multiplexer_96_out), .out(multiplexer_124_out), .sel(Shift[3]));
  Multiplexer multiplexer_125 (.in0(multiplexer_90_out), .in1(1'b0), .out(multiplexer_125_out), .sel(Shift[3]));
  Multiplexer multiplexer_126 (.in0(multiplexer_92_out), .in1(1'b0), .out(multiplexer_126_out), .sel(Shift[3]));
  Multiplexer multiplexer_127 (.in0(multiplexer_94_out), .in1(1'b0), .out(multiplexer_127_out), .sel(Shift[3]));
  Multiplexer multiplexer_128 (.in0(multiplexer_96_out), .in1(1'b0), .out(multiplexer_128_out), .sel(Shift[3]));
  Multiplexer multiplexer_129 (.in0(multiplexer_97_out), .in1(multiplexer_105_out), .out(out_3[0]), .sel(Shift[4]));
  Multiplexer multiplexer_130 (.in0(multiplexer_98_out), .in1(multiplexer_106_out), .out(out_3[2]), .sel(Shift[4]));
  Multiplexer multiplexer_131 (.in0(multiplexer_99_out), .in1(multiplexer_107_out), .out(out_3[4]), .sel(Shift[4]));
  Multiplexer multiplexer_132 (.in0(multiplexer_100_out), .in1(multiplexer_108_out), .out(out_3[6]), .sel(Shift[4]));
  Multiplexer multiplexer_133 (.in0(multiplexer_101_out), .in1(multiplexer_109_out), .out(out_3[8]), .sel(Shift[4]));
  Multiplexer multiplexer_134 (.in0(multiplexer_102_out), .in1(multiplexer_110_out), .out(out_3[10]), .sel(Shift[4]));
  Multiplexer multiplexer_135 (.in0(multiplexer_103_out), .in1(multiplexer_111_out), .out(out_3[12]), .sel(Shift[4]));
  Multiplexer multiplexer_136 (.in0(multiplexer_104_out), .in1(multiplexer_112_out), .out(out_3[14]), .sel(Shift[4]));
  Multiplexer multiplexer_137 (.in0(multiplexer_105_out), .in1(1'b0), .out(out_3[16]), .sel(Shift[4]));
  Multiplexer multiplexer_138 (.in0(multiplexer_106_out), .in1(1'b0), .out(out_3[18]), .sel(Shift[4]));
  Multiplexer multiplexer_139 (.in0(multiplexer_107_out), .in1(1'b0), .out(out_3[20]), .sel(Shift[4]));
  Multiplexer multiplexer_140 (.in0(multiplexer_108_out), .in1(1'b0), .out(out_3[22]), .sel(Shift[4]));
  Multiplexer multiplexer_141 (.in0(multiplexer_109_out), .in1(1'b0), .out(out_3[24]), .sel(Shift[4]));
  Multiplexer multiplexer_142 (.in0(multiplexer_110_out), .in1(1'b0), .out(out_3[26]), .sel(Shift[4]));
  Multiplexer multiplexer_143 (.in0(multiplexer_111_out), .in1(1'b0), .out(out_3[28]), .sel(Shift[4]));
  Multiplexer multiplexer_144 (.in0(multiplexer_112_out), .in1(1'b0), .out(out_3[30]), .sel(Shift[4]));
  Multiplexer multiplexer_145 (.in0(multiplexer_113_out), .in1(multiplexer_121_out), .out(out_3[1]), .sel(Shift[4]));
  Multiplexer multiplexer_146 (.in0(multiplexer_114_out), .in1(multiplexer_122_out), .out(out_3[3]), .sel(Shift[4]));
  Multiplexer multiplexer_147 (.in0(multiplexer_115_out), .in1(multiplexer_123_out), .out(out_3[5]), .sel(Shift[4]));
  Multiplexer multiplexer_148 (.in0(multiplexer_116_out), .in1(multiplexer_124_out), .out(out_3[7]), .sel(Shift[4]));
  Multiplexer multiplexer_149 (.in0(multiplexer_117_out), .in1(multiplexer_125_out), .out(out_3[9]), .sel(Shift[4]));
  Multiplexer multiplexer_150 (.in0(multiplexer_118_out), .in1(multiplexer_126_out), .out(out_3[11]), .sel(Shift[4]));
  Multiplexer multiplexer_151 (.in0(multiplexer_119_out), .in1(multiplexer_127_out), .out(out_3[13]), .sel(Shift[4]));
  Multiplexer multiplexer_152 (.in0(multiplexer_120_out), .in1(multiplexer_128_out), .out(out_3[15]), .sel(Shift[4]));
  Multiplexer multiplexer_153 (.in0(multiplexer_121_out), .in1(1'b0), .out(out_3[17]), .sel(Shift[4]));
  Multiplexer multiplexer_154 (.in0(multiplexer_122_out), .in1(1'b0), .out(out_3[19]), .sel(Shift[4]));
  Multiplexer multiplexer_155 (.in0(multiplexer_123_out), .in1(1'b0), .out(out_3[21]), .sel(Shift[4]));
  Multiplexer multiplexer_156 (.in0(multiplexer_124_out), .in1(1'b0), .out(out_3[23]), .sel(Shift[4]));
  Multiplexer multiplexer_157 (.in0(multiplexer_125_out), .in1(1'b0), .out(out_3[25]), .sel(Shift[4]));
  Multiplexer multiplexer_158 (.in0(multiplexer_126_out), .in1(1'b0), .out(out_3[27]), .sel(Shift[4]));
  Multiplexer multiplexer_159 (.in0(multiplexer_127_out), .in1(1'b0), .out(out_3[29]), .sel(Shift[4]));
  Multiplexer multiplexer_160 (.in0(multiplexer_128_out), .in1(1'b0), .out(out_3[31]), .sel(Shift[4]));
endmodule
module V_LSL_32bit (
  input  [31:0] in_1,
  input  [4:0] Shift,
  output [31:0] out_3
);

  wire multiplexer_1_out, multiplexer_2_out, multiplexer_3_out, multiplexer_4_out, multiplexer_5_out,
       multiplexer_6_out, multiplexer_7_out, multiplexer_8_out, multiplexer_9_out, multiplexer_10_out,
       multiplexer_11_out, multiplexer_12_out, multiplexer_13_out, multiplexer_14_out, multiplexer_15_out,
       multiplexer_16_out, multiplexer_17_out, multiplexer_18_out, multiplexer_19_out, multiplexer_20_out,
       multiplexer_21_out, multiplexer_22_out, multiplexer_23_out, multiplexer_24_out, multiplexer_25_out,
       multiplexer_26_out, multiplexer_27_out, multiplexer_28_out, multiplexer_29_out, multiplexer_30_out,
       multiplexer_31_out, multiplexer_32_out, multiplexer_33_out, multiplexer_34_out, multiplexer_35_out,
       multiplexer_36_out, multiplexer_37_out, multiplexer_38_out, multiplexer_39_out, multiplexer_40_out,
       multiplexer_41_out, multiplexer_42_out, multiplexer_43_out, multiplexer_44_out, multiplexer_45_out,
       multiplexer_46_out, multiplexer_47_out, multiplexer_48_out, multiplexer_49_out, multiplexer_50_out,
       multiplexer_51_out, multiplexer_52_out, multiplexer_53_out, multiplexer_54_out, multiplexer_55_out,
       multiplexer_56_out, multiplexer_57_out, multiplexer_58_out, multiplexer_59_out, multiplexer_60_out,
       multiplexer_61_out, multiplexer_62_out, multiplexer_63_out, multiplexer_64_out, multiplexer_65_out,
       multiplexer_66_out, multiplexer_67_out, multiplexer_68_out, multiplexer_69_out, multiplexer_70_out,
       multiplexer_71_out, multiplexer_72_out, multiplexer_73_out, multiplexer_74_out, multiplexer_75_out,
       multiplexer_76_out, multiplexer_77_out, multiplexer_78_out, multiplexer_79_out, multiplexer_80_out,
       multiplexer_81_out, multiplexer_82_out, multiplexer_83_out, multiplexer_84_out, multiplexer_85_out,
       multiplexer_86_out, multiplexer_87_out, multiplexer_88_out, multiplexer_89_out, multiplexer_90_out,
       multiplexer_91_out, multiplexer_92_out, multiplexer_93_out, multiplexer_94_out, multiplexer_95_out,
       multiplexer_96_out, multiplexer_97_out, multiplexer_98_out, multiplexer_99_out, multiplexer_100_out,
       multiplexer_101_out, multiplexer_102_out, multiplexer_103_out, multiplexer_104_out,
       multiplexer_105_out, multiplexer_106_out, multiplexer_107_out, multiplexer_108_out,
       multiplexer_109_out, multiplexer_110_out, multiplexer_111_out, multiplexer_112_out,
       multiplexer_113_out, multiplexer_114_out, multiplexer_115_out, multiplexer_116_out,
       multiplexer_117_out, multiplexer_118_out, multiplexer_119_out, multiplexer_120_out,
       multiplexer_121_out, multiplexer_122_out, multiplexer_123_out, multiplexer_124_out,
       multiplexer_125_out, multiplexer_126_out, multiplexer_127_out, multiplexer_128_out;

  Multiplexer multiplexer_1 (.in0(in_1[31]), .in1(in_1[30]), .out(multiplexer_1_out), .sel(Shift[0]));
  Multiplexer multiplexer_2 (.in0(in_1[29]), .in1(in_1[28]), .out(multiplexer_2_out), .sel(Shift[0]));
  Multiplexer multiplexer_3 (.in0(in_1[27]), .in1(in_1[26]), .out(multiplexer_3_out), .sel(Shift[0]));
  Multiplexer multiplexer_4 (.in0(in_1[25]), .in1(in_1[24]), .out(multiplexer_4_out), .sel(Shift[0]));
  Multiplexer multiplexer_5 (.in0(in_1[23]), .in1(in_1[22]), .out(multiplexer_5_out), .sel(Shift[0]));
  Multiplexer multiplexer_6 (.in0(in_1[21]), .in1(in_1[20]), .out(multiplexer_6_out), .sel(Shift[0]));
  Multiplexer multiplexer_7 (.in0(in_1[19]), .in1(in_1[18]), .out(multiplexer_7_out), .sel(Shift[0]));
  Multiplexer multiplexer_8 (.in0(in_1[17]), .in1(in_1[16]), .out(multiplexer_8_out), .sel(Shift[0]));
  Multiplexer multiplexer_9 (.in0(in_1[15]), .in1(in_1[14]), .out(multiplexer_9_out), .sel(Shift[0]));
  Multiplexer multiplexer_10 (.in0(in_1[13]), .in1(in_1[12]), .out(multiplexer_10_out), .sel(Shift[0]));
  Multiplexer multiplexer_11 (.in0(in_1[11]), .in1(in_1[10]), .out(multiplexer_11_out), .sel(Shift[0]));
  Multiplexer multiplexer_12 (.in0(in_1[9]), .in1(in_1[8]), .out(multiplexer_12_out), .sel(Shift[0]));
  Multiplexer multiplexer_13 (.in0(in_1[7]), .in1(in_1[6]), .out(multiplexer_13_out), .sel(Shift[0]));
  Multiplexer multiplexer_14 (.in0(in_1[5]), .in1(in_1[4]), .out(multiplexer_14_out), .sel(Shift[0]));
  Multiplexer multiplexer_15 (.in0(in_1[3]), .in1(in_1[2]), .out(multiplexer_15_out), .sel(Shift[0]));
  Multiplexer multiplexer_16 (.in0(in_1[1]), .in1(in_1[0]), .out(multiplexer_16_out), .sel(Shift[0]));
  Multiplexer multiplexer_17 (.in0(in_1[30]), .in1(in_1[29]), .out(multiplexer_17_out), .sel(Shift[0]));
  Multiplexer multiplexer_18 (.in0(in_1[28]), .in1(in_1[27]), .out(multiplexer_18_out), .sel(Shift[0]));
  Multiplexer multiplexer_19 (.in0(in_1[26]), .in1(in_1[25]), .out(multiplexer_19_out), .sel(Shift[0]));
  Multiplexer multiplexer_20 (.in0(in_1[24]), .in1(in_1[23]), .out(multiplexer_20_out), .sel(Shift[0]));
  Multiplexer multiplexer_21 (.in0(in_1[22]), .in1(in_1[21]), .out(multiplexer_21_out), .sel(Shift[0]));
  Multiplexer multiplexer_22 (.in0(in_1[20]), .in1(in_1[19]), .out(multiplexer_22_out), .sel(Shift[0]));
  Multiplexer multiplexer_23 (.in0(in_1[18]), .in1(in_1[17]), .out(multiplexer_23_out), .sel(Shift[0]));
  Multiplexer multiplexer_24 (.in0(in_1[16]), .in1(in_1[15]), .out(multiplexer_24_out), .sel(Shift[0]));
  Multiplexer multiplexer_25 (.in0(in_1[14]), .in1(in_1[13]), .out(multiplexer_25_out), .sel(Shift[0]));
  Multiplexer multiplexer_26 (.in0(in_1[12]), .in1(in_1[11]), .out(multiplexer_26_out), .sel(Shift[0]));
  Multiplexer multiplexer_27 (.in0(in_1[10]), .in1(in_1[9]), .out(multiplexer_27_out), .sel(Shift[0]));
  Multiplexer multiplexer_28 (.in0(in_1[8]), .in1(in_1[7]), .out(multiplexer_28_out), .sel(Shift[0]));
  Multiplexer multiplexer_29 (.in0(in_1[6]), .in1(in_1[5]), .out(multiplexer_29_out), .sel(Shift[0]));
  Multiplexer multiplexer_30 (.in0(in_1[4]), .in1(in_1[3]), .out(multiplexer_30_out), .sel(Shift[0]));
  Multiplexer multiplexer_31 (.in0(in_1[2]), .in1(in_1[1]), .out(multiplexer_31_out), .sel(Shift[0]));
  Multiplexer multiplexer_32 (.in0(in_1[0]), .in1(1'b0), .out(multiplexer_32_out), .sel(Shift[0]));
  Multiplexer multiplexer_33 (
    .in0(multiplexer_1_out), .in1(multiplexer_2_out), .out(multiplexer_33_out), .sel(Shift[1]));
  Multiplexer multiplexer_34 (
    .in0(multiplexer_2_out), .in1(multiplexer_3_out), .out(multiplexer_34_out), .sel(Shift[1]));
  Multiplexer multiplexer_35 (
    .in0(multiplexer_3_out), .in1(multiplexer_4_out), .out(multiplexer_35_out), .sel(Shift[1]));
  Multiplexer multiplexer_36 (
    .in0(multiplexer_4_out), .in1(multiplexer_5_out), .out(multiplexer_36_out), .sel(Shift[1]));
  Multiplexer multiplexer_37 (
    .in0(multiplexer_5_out), .in1(multiplexer_7_out), .out(multiplexer_37_out), .sel(Shift[1]));
  Multiplexer multiplexer_38 (
    .in0(multiplexer_6_out), .in1(multiplexer_7_out), .out(multiplexer_38_out), .sel(Shift[1]));
  Multiplexer multiplexer_39 (
    .in0(multiplexer_7_out), .in1(multiplexer_8_out), .out(multiplexer_39_out), .sel(Shift[1]));
  Multiplexer multiplexer_40 (
    .in0(multiplexer_8_out), .in1(multiplexer_9_out), .out(multiplexer_40_out), .sel(Shift[1]));
  Multiplexer multiplexer_41 (
    .in0(multiplexer_9_out), .in1(multiplexer_10_out), .out(multiplexer_41_out), .sel(Shift[1]));
  Multiplexer multiplexer_42 (
    .in0(multiplexer_10_out), .in1(multiplexer_11_out), .out(multiplexer_42_out), .sel(Shift[1]));
  Multiplexer multiplexer_43 (
    .in0(multiplexer_11_out), .in1(multiplexer_12_out), .out(multiplexer_43_out), .sel(Shift[1]));
  Multiplexer multiplexer_44 (
    .in0(multiplexer_12_out), .in1(multiplexer_13_out), .out(multiplexer_44_out), .sel(Shift[1]));
  Multiplexer multiplexer_45 (
    .in0(multiplexer_13_out), .in1(multiplexer_14_out), .out(multiplexer_45_out), .sel(Shift[1]));
  Multiplexer multiplexer_46 (
    .in0(multiplexer_14_out), .in1(multiplexer_15_out), .out(multiplexer_46_out), .sel(Shift[1]));
  Multiplexer multiplexer_47 (
    .in0(multiplexer_15_out), .in1(multiplexer_16_out), .out(multiplexer_47_out), .sel(Shift[1]));
  Multiplexer multiplexer_48 (.in0(multiplexer_16_out), .in1(1'b0), .out(multiplexer_48_out), .sel(Shift[1]));
  Multiplexer multiplexer_49 (
    .in0(multiplexer_17_out), .in1(multiplexer_18_out), .out(multiplexer_49_out), .sel(Shift[1]));
  Multiplexer multiplexer_50 (
    .in0(multiplexer_18_out), .in1(multiplexer_19_out), .out(multiplexer_50_out), .sel(Shift[1]));
  Multiplexer multiplexer_51 (
    .in0(multiplexer_19_out), .in1(multiplexer_20_out), .out(multiplexer_51_out), .sel(Shift[1]));
  Multiplexer multiplexer_52 (
    .in0(multiplexer_20_out), .in1(multiplexer_21_out), .out(multiplexer_52_out), .sel(Shift[1]));
  Multiplexer multiplexer_53 (
    .in0(multiplexer_21_out), .in1(multiplexer_22_out), .out(multiplexer_53_out), .sel(Shift[1]));
  Multiplexer multiplexer_54 (
    .in0(multiplexer_22_out), .in1(multiplexer_23_out), .out(multiplexer_54_out), .sel(Shift[1]));
  Multiplexer multiplexer_55 (
    .in0(multiplexer_23_out), .in1(multiplexer_24_out), .out(multiplexer_55_out), .sel(Shift[1]));
  Multiplexer multiplexer_56 (
    .in0(multiplexer_24_out), .in1(multiplexer_25_out), .out(multiplexer_56_out), .sel(Shift[1]));
  Multiplexer multiplexer_57 (
    .in0(multiplexer_25_out), .in1(multiplexer_26_out), .out(multiplexer_57_out), .sel(Shift[1]));
  Multiplexer multiplexer_58 (
    .in0(multiplexer_26_out), .in1(multiplexer_27_out), .out(multiplexer_58_out), .sel(Shift[1]));
  Multiplexer multiplexer_59 (
    .in0(multiplexer_27_out), .in1(multiplexer_28_out), .out(multiplexer_59_out), .sel(Shift[1]));
  Multiplexer multiplexer_60 (
    .in0(multiplexer_28_out), .in1(multiplexer_29_out), .out(multiplexer_60_out), .sel(Shift[1]));
  Multiplexer multiplexer_61 (
    .in0(multiplexer_29_out), .in1(multiplexer_30_out), .out(multiplexer_61_out), .sel(Shift[1]));
  Multiplexer multiplexer_62 (
    .in0(multiplexer_30_out), .in1(multiplexer_31_out), .out(multiplexer_62_out), .sel(Shift[1]));
  Multiplexer multiplexer_63 (
    .in0(multiplexer_31_out), .in1(multiplexer_32_out), .out(multiplexer_63_out), .sel(Shift[1]));
  Multiplexer multiplexer_64 (.in0(multiplexer_32_out), .in1(1'b0), .out(multiplexer_64_out), .sel(Shift[1]));
  Multiplexer multiplexer_65 (
    .in0(multiplexer_33_out), .in1(multiplexer_35_out), .out(multiplexer_65_out), .sel(Shift[2]));
  Multiplexer multiplexer_66 (
    .in0(multiplexer_49_out), .in1(multiplexer_51_out), .out(multiplexer_66_out), .sel(Shift[2]));
  Multiplexer multiplexer_67 (
    .in0(multiplexer_34_out), .in1(multiplexer_36_out), .out(multiplexer_67_out), .sel(Shift[2]));
  Multiplexer multiplexer_68 (
    .in0(multiplexer_50_out), .in1(multiplexer_52_out), .out(multiplexer_68_out), .sel(Shift[2]));
  Multiplexer multiplexer_69 (
    .in0(multiplexer_35_out), .in1(multiplexer_37_out), .out(multiplexer_69_out), .sel(Shift[2]));
  Multiplexer multiplexer_70 (
    .in0(multiplexer_51_out), .in1(multiplexer_53_out), .out(multiplexer_70_out), .sel(Shift[2]));
  Multiplexer multiplexer_71 (
    .in0(multiplexer_36_out), .in1(multiplexer_38_out), .out(multiplexer_71_out), .sel(Shift[2]));
  Multiplexer multiplexer_72 (
    .in0(multiplexer_52_out), .in1(multiplexer_54_out), .out(multiplexer_72_out), .sel(Shift[2]));
  Multiplexer multiplexer_73 (
    .in0(multiplexer_37_out), .in1(multiplexer_39_out), .out(multiplexer_73_out), .sel(Shift[2]));
  Multiplexer multiplexer_74 (
    .in0(multiplexer_53_out), .in1(multiplexer_55_out), .out(multiplexer_74_out), .sel(Shift[2]));
  Multiplexer multiplexer_75 (
    .in0(multiplexer_38_out), .in1(multiplexer_40_out), .out(multiplexer_75_out), .sel(Shift[2]));
  Multiplexer multiplexer_76 (
    .in0(multiplexer_54_out), .in1(multiplexer_56_out), .out(multiplexer_76_out), .sel(Shift[2]));
  Multiplexer multiplexer_77 (
    .in0(multiplexer_39_out), .in1(multiplexer_41_out), .out(multiplexer_77_out), .sel(Shift[2]));
  Multiplexer multiplexer_78 (
    .in0(multiplexer_55_out), .in1(multiplexer_57_out), .out(multiplexer_78_out), .sel(Shift[2]));
  Multiplexer multiplexer_79 (
    .in0(multiplexer_40_out), .in1(multiplexer_42_out), .out(multiplexer_79_out), .sel(Shift[2]));
  Multiplexer multiplexer_80 (
    .in0(multiplexer_56_out), .in1(multiplexer_58_out), .out(multiplexer_80_out), .sel(Shift[2]));
  Multiplexer multiplexer_81 (
    .in0(multiplexer_41_out), .in1(multiplexer_43_out), .out(multiplexer_81_out), .sel(Shift[2]));
  Multiplexer multiplexer_82 (
    .in0(multiplexer_57_out), .in1(multiplexer_59_out), .out(multiplexer_82_out), .sel(Shift[2]));
  Multiplexer multiplexer_83 (
    .in0(multiplexer_42_out), .in1(multiplexer_44_out), .out(multiplexer_83_out), .sel(Shift[2]));
  Multiplexer multiplexer_84 (
    .in0(multiplexer_58_out), .in1(multiplexer_60_out), .out(multiplexer_84_out), .sel(Shift[2]));
  Multiplexer multiplexer_85 (
    .in0(multiplexer_43_out), .in1(multiplexer_45_out), .out(multiplexer_85_out), .sel(Shift[2]));
  Multiplexer multiplexer_86 (
    .in0(multiplexer_59_out), .in1(multiplexer_61_out), .out(multiplexer_86_out), .sel(Shift[2]));
  Multiplexer multiplexer_87 (
    .in0(multiplexer_44_out), .in1(multiplexer_46_out), .out(multiplexer_87_out), .sel(Shift[2]));
  Multiplexer multiplexer_88 (
    .in0(multiplexer_60_out), .in1(multiplexer_62_out), .out(multiplexer_88_out), .sel(Shift[2]));
  Multiplexer multiplexer_89 (
    .in0(multiplexer_45_out), .in1(multiplexer_47_out), .out(multiplexer_89_out), .sel(Shift[2]));
  Multiplexer multiplexer_90 (
    .in0(multiplexer_61_out), .in1(multiplexer_63_out), .out(multiplexer_90_out), .sel(Shift[2]));
  Multiplexer multiplexer_91 (
    .in0(multiplexer_46_out), .in1(multiplexer_48_out), .out(multiplexer_91_out), .sel(Shift[2]));
  Multiplexer multiplexer_92 (
    .in0(multiplexer_62_out), .in1(multiplexer_64_out), .out(multiplexer_92_out), .sel(Shift[2]));
  Multiplexer multiplexer_93 (.in0(multiplexer_47_out), .in1(1'b0), .out(multiplexer_93_out), .sel(Shift[2]));
  Multiplexer multiplexer_94 (.in0(multiplexer_63_out), .in1(1'b0), .out(multiplexer_94_out), .sel(Shift[2]));
  Multiplexer multiplexer_95 (.in0(multiplexer_48_out), .in1(1'b0), .out(multiplexer_95_out), .sel(Shift[2]));
  Multiplexer multiplexer_96 (.in0(multiplexer_64_out), .in1(1'b0), .out(multiplexer_96_out), .sel(Shift[2]));
  Multiplexer multiplexer_97 (
    .in0(multiplexer_65_out), .in1(multiplexer_73_out), .out(multiplexer_97_out), .sel(Shift[3]));
  Multiplexer multiplexer_98 (
    .in0(multiplexer_67_out), .in1(multiplexer_75_out), .out(multiplexer_98_out), .sel(Shift[3]));
  Multiplexer multiplexer_99 (
    .in0(multiplexer_69_out), .in1(multiplexer_77_out), .out(multiplexer_99_out), .sel(Shift[3]));
  Multiplexer multiplexer_100 (
    .in0(multiplexer_71_out), .in1(multiplexer_79_out), .out(multiplexer_100_out), .sel(Shift[3]));
  Multiplexer multiplexer_101 (
    .in0(multiplexer_73_out), .in1(multiplexer_81_out), .out(multiplexer_101_out), .sel(Shift[3]));
  Multiplexer multiplexer_102 (
    .in0(multiplexer_75_out), .in1(multiplexer_83_out), .out(multiplexer_102_out), .sel(Shift[3]));
  Multiplexer multiplexer_103 (
    .in0(multiplexer_77_out), .in1(multiplexer_85_out), .out(multiplexer_103_out), .sel(Shift[3]));
  Multiplexer multiplexer_104 (
    .in0(multiplexer_79_out), .in1(multiplexer_87_out), .out(multiplexer_104_out), .sel(Shift[3]));
  Multiplexer multiplexer_105 (
    .in0(multiplexer_81_out), .in1(multiplexer_89_out), .out(multiplexer_105_out), .sel(Shift[3]));
  Multiplexer multiplexer_106 (
    .in0(multiplexer_83_out), .in1(multiplexer_91_out), .out(multiplexer_106_out), .sel(Shift[3]));
  Multiplexer multiplexer_107 (
    .in0(multiplexer_85_out), .in1(multiplexer_93_out), .out(multiplexer_107_out), .sel(Shift[3]));
  Multiplexer multiplexer_108 (
    .in0(multiplexer_87_out), .in1(multiplexer_95_out), .out(multiplexer_108_out), .sel(Shift[3]));
  Multiplexer multiplexer_109 (.in0(multiplexer_89_out), .in1(1'b0), .out(multiplexer_109_out), .sel(Shift[3]));
  Multiplexer multiplexer_110 (.in0(multiplexer_91_out), .in1(1'b0), .out(multiplexer_110_out), .sel(Shift[3]));
  Multiplexer multiplexer_111 (.in0(multiplexer_93_out), .in1(1'b0), .out(multiplexer_111_out), .sel(Shift[3]));
  Multiplexer multiplexer_112 (.in0(multiplexer_95_out), .in1(1'b0), .out(multiplexer_112_out), .sel(Shift[3]));
  Multiplexer multiplexer_113 (
    .in0(multiplexer_66_out), .in1(multiplexer_74_out), .out(multiplexer_113_out), .sel(Shift[3]));
  Multiplexer multiplexer_114 (
    .in0(multiplexer_68_out), .in1(multiplexer_76_out), .out(multiplexer_114_out), .sel(Shift[3]));
  Multiplexer multiplexer_115 (
    .in0(multiplexer_70_out), .in1(multiplexer_78_out), .out(multiplexer_115_out), .sel(Shift[3]));
  Multiplexer multiplexer_116 (
    .in0(multiplexer_72_out), .in1(multiplexer_80_out), .out(multiplexer_116_out), .sel(Shift[3]));
  Multiplexer multiplexer_117 (
    .in0(multiplexer_74_out), .in1(multiplexer_82_out), .out(multiplexer_117_out), .sel(Shift[3]));
  Multiplexer multiplexer_118 (
    .in0(multiplexer_76_out), .in1(multiplexer_84_out), .out(multiplexer_118_out), .sel(Shift[3]));
  Multiplexer multiplexer_119 (
    .in0(multiplexer_78_out), .in1(multiplexer_86_out), .out(multiplexer_119_out), .sel(Shift[3]));
  Multiplexer multiplexer_120 (
    .in0(multiplexer_80_out), .in1(multiplexer_88_out), .out(multiplexer_120_out), .sel(Shift[3]));
  Multiplexer multiplexer_121 (
    .in0(multiplexer_82_out), .in1(multiplexer_90_out), .out(multiplexer_121_out), .sel(Shift[3]));
  Multiplexer multiplexer_122 (
    .in0(multiplexer_84_out), .in1(multiplexer_92_out), .out(multiplexer_122_out), .sel(Shift[3]));
  Multiplexer multiplexer_123 (
    .in0(multiplexer_86_out), .in1(multiplexer_94_out), .out(multiplexer_123_out), .sel(Shift[3]));
  Multiplexer multiplexer_124 (
    .in0(multiplexer_88_out), .in1(multiplexer_96_out), .out(multiplexer_124_out), .sel(Shift[3]));
  Multiplexer multiplexer_125 (.in0(multiplexer_90_out), .in1(1'b0), .out(multiplexer_125_out), .sel(Shift[3]));
  Multiplexer multiplexer_126 (.in0(multiplexer_92_out), .in1(1'b0), .out(multiplexer_126_out), .sel(Shift[3]));
  Multiplexer multiplexer_127 (.in0(multiplexer_94_out), .in1(1'b0), .out(multiplexer_127_out), .sel(Shift[3]));
  Multiplexer multiplexer_128 (.in0(multiplexer_96_out), .in1(1'b0), .out(multiplexer_128_out), .sel(Shift[3]));
  Multiplexer multiplexer_129 (.in0(multiplexer_97_out), .in1(multiplexer_105_out), .out(out_3[31]), .sel(Shift[4]));
  Multiplexer multiplexer_130 (.in0(multiplexer_98_out), .in1(multiplexer_106_out), .out(out_3[29]), .sel(Shift[4]));
  Multiplexer multiplexer_131 (.in0(multiplexer_99_out), .in1(multiplexer_107_out), .out(out_3[27]), .sel(Shift[4]));
  Multiplexer multiplexer_132 (.in0(multiplexer_100_out), .in1(multiplexer_108_out), .out(out_3[25]), .sel(Shift[4]));
  Multiplexer multiplexer_133 (.in0(multiplexer_101_out), .in1(multiplexer_109_out), .out(out_3[23]), .sel(Shift[4]));
  Multiplexer multiplexer_134 (.in0(multiplexer_102_out), .in1(multiplexer_110_out), .out(out_3[21]), .sel(Shift[4]));
  Multiplexer multiplexer_135 (.in0(multiplexer_103_out), .in1(multiplexer_111_out), .out(out_3[19]), .sel(Shift[4]));
  Multiplexer multiplexer_136 (.in0(multiplexer_104_out), .in1(multiplexer_112_out), .out(out_3[17]), .sel(Shift[4]));
  Multiplexer multiplexer_137 (.in0(multiplexer_105_out), .in1(1'b0), .out(out_3[15]), .sel(Shift[4]));
  Multiplexer multiplexer_138 (.in0(multiplexer_106_out), .in1(1'b0), .out(out_3[13]), .sel(Shift[4]));
  Multiplexer multiplexer_139 (.in0(multiplexer_107_out), .in1(1'b0), .out(out_3[11]), .sel(Shift[4]));
  Multiplexer multiplexer_140 (.in0(multiplexer_108_out), .in1(1'b0), .out(out_3[9]), .sel(Shift[4]));
  Multiplexer multiplexer_141 (.in0(multiplexer_109_out), .in1(1'b0), .out(out_3[7]), .sel(Shift[4]));
  Multiplexer multiplexer_142 (.in0(multiplexer_110_out), .in1(1'b0), .out(out_3[5]), .sel(Shift[4]));
  Multiplexer multiplexer_143 (.in0(multiplexer_111_out), .in1(1'b0), .out(out_3[3]), .sel(Shift[4]));
  Multiplexer multiplexer_144 (.in0(multiplexer_112_out), .in1(1'b0), .out(out_3[1]), .sel(Shift[4]));
  Multiplexer multiplexer_145 (.in0(multiplexer_113_out), .in1(multiplexer_121_out), .out(out_3[30]), .sel(Shift[4]));
  Multiplexer multiplexer_146 (.in0(multiplexer_114_out), .in1(multiplexer_122_out), .out(out_3[28]), .sel(Shift[4]));
  Multiplexer multiplexer_147 (.in0(multiplexer_115_out), .in1(multiplexer_123_out), .out(out_3[26]), .sel(Shift[4]));
  Multiplexer multiplexer_148 (.in0(multiplexer_116_out), .in1(multiplexer_124_out), .out(out_3[24]), .sel(Shift[4]));
  Multiplexer multiplexer_149 (.in0(multiplexer_117_out), .in1(multiplexer_125_out), .out(out_3[22]), .sel(Shift[4]));
  Multiplexer multiplexer_150 (.in0(multiplexer_118_out), .in1(multiplexer_126_out), .out(out_3[20]), .sel(Shift[4]));
  Multiplexer multiplexer_151 (.in0(multiplexer_119_out), .in1(multiplexer_127_out), .out(out_3[18]), .sel(Shift[4]));
  Multiplexer multiplexer_152 (.in0(multiplexer_120_out), .in1(multiplexer_128_out), .out(out_3[16]), .sel(Shift[4]));
  Multiplexer multiplexer_153 (.in0(multiplexer_121_out), .in1(1'b0), .out(out_3[14]), .sel(Shift[4]));
  Multiplexer multiplexer_154 (.in0(multiplexer_122_out), .in1(1'b0), .out(out_3[12]), .sel(Shift[4]));
  Multiplexer multiplexer_155 (.in0(multiplexer_123_out), .in1(1'b0), .out(out_3[10]), .sel(Shift[4]));
  Multiplexer multiplexer_156 (.in0(multiplexer_124_out), .in1(1'b0), .out(out_3[8]), .sel(Shift[4]));
  Multiplexer multiplexer_157 (.in0(multiplexer_125_out), .in1(1'b0), .out(out_3[6]), .sel(Shift[4]));
  Multiplexer multiplexer_158 (.in0(multiplexer_126_out), .in1(1'b0), .out(out_3[4]), .sel(Shift[4]));
  Multiplexer multiplexer_159 (.in0(multiplexer_127_out), .in1(1'b0), .out(out_3[2]), .sel(Shift[4]));
  Multiplexer multiplexer_160 (.in0(multiplexer_128_out), .in1(1'b0), .out(out_3[0]), .sel(Shift[4]));
endmodule

module Add_3_4bit (
  input  [3:0] A,
  output [3:0] F
);

  wire equivalence_4bit_1_less, not_1_out;
  wire [3:0] add_4bit_1_add4;

  Add_4bit add_4bit_1 (.A(A), .B(4'b0011), .ADD4(add_4bit_1_add4));  // open: Cin, Cout
  not not_1 (not_1_out, equivalence_4bit_1_less);
  Equivalence_4bit equivalence_4bit_1 (.A(A), .B(4'b0101), .Less(equivalence_4bit_1_less));  // open: Equal, Greater
  Multiplexer #(.width(4)) multiplexer_1 (.in0(A), .in1(add_4bit_1_add4), .out(F), .sel(not_1_out));
endmodule

module Double_Dabble_32bit (
  input  [31:0] in_1,
  output [3:0] OB,
  output [3:0] HM,
  output [3:0] TM,
  output [3:0] OM,
  output [3:0] HT,
  output [3:0] TT,
  output [3:0] OT,
  output [3:0] H,
  output [3:0] T,
  output [3:0] O
);

  wire [3:0] add_3_4bit_30_f, add_3_4bit_31_f, add_3_4bit_32_f, add_3_4bit_33_f, add_3_4bit_34_f,
       add_3_4bit_35_f, add_3_4bit_36_f, add_3_4bit_37_f, add_3_4bit_38_f, add_3_4bit_39_f, add_3_4bit_40_f,
       add_3_4bit_41_f, add_3_4bit_42_f, add_3_4bit_43_f, add_3_4bit_44_f, add_3_4bit_45_f, add_3_4bit_46_f,
       add_3_4bit_47_f, add_3_4bit_48_f, add_3_4bit_49_f, add_3_4bit_50_f, add_3_4bit_51_f, add_3_4bit_52_f,
       add_3_4bit_53_f, add_3_4bit_54_f;
  wire [3:1] add_3_4bit_1_f, add_3_4bit_2_f, add_3_4bit_3_f, add_3_4bit_4_f, add_3_4bit_5_f, add_3_4bit_6_f,
       add_3_4bit_7_f, add_3_4bit_8_f, add_3_4bit_9_f, add_3_4bit_10_f, add_3_4bit_11_f, add_3_4bit_12_f,
       add_3_4bit_13_f, add_3_4bit_14_f, add_3_4bit_15_f, add_3_4bit_16_f, add_3_4bit_17_f, add_3_4bit_18_f,
       add_3_4bit_19_f, add_3_4bit_20_f, add_3_4bit_21_f, add_3_4bit_22_f, add_3_4bit_23_f, add_3_4bit_24_f,
       add_3_4bit_25_f, add_3_4bit_26_f, add_3_4bit_27_f, add_3_4bit_28_f, add_3_4bit_56_f, add_3_4bit_57_f,
       add_3_4bit_58_f, add_3_4bit_59_f, add_3_4bit_60_f, add_3_4bit_61_f, add_3_4bit_62_f, add_3_4bit_63_f,
       add_3_4bit_64_f, add_3_4bit_65_f, add_3_4bit_66_f, add_3_4bit_67_f, add_3_4bit_68_f, add_3_4bit_69_f,
       add_3_4bit_70_f, add_3_4bit_71_f, add_3_4bit_72_f, add_3_4bit_73_f, add_3_4bit_74_f, add_3_4bit_75_f,
       add_3_4bit_76_f, add_3_4bit_77_f, add_3_4bit_79_f, add_3_4bit_80_f, add_3_4bit_81_f, add_3_4bit_82_f,
       add_3_4bit_83_f, add_3_4bit_84_f, add_3_4bit_85_f, add_3_4bit_86_f, add_3_4bit_87_f, add_3_4bit_88_f,
       add_3_4bit_89_f, add_3_4bit_90_f, add_3_4bit_91_f, add_3_4bit_92_f, add_3_4bit_93_f, add_3_4bit_94_f,
       add_3_4bit_95_f, add_3_4bit_96_f, add_3_4bit_97_f, add_3_4bit_99_f, add_3_4bit_100_f,
       add_3_4bit_101_f, add_3_4bit_102_f, add_3_4bit_103_f, add_3_4bit_104_f, add_3_4bit_105_f,
       add_3_4bit_106_f, add_3_4bit_107_f, add_3_4bit_108_f, add_3_4bit_109_f, add_3_4bit_110_f,
       add_3_4bit_111_f, add_3_4bit_112_f, add_3_4bit_113_f, add_3_4bit_114_f, add_3_4bit_116_f,
       add_3_4bit_117_f, add_3_4bit_118_f, add_3_4bit_119_f, add_3_4bit_120_f, add_3_4bit_121_f,
       add_3_4bit_122_f, add_3_4bit_123_f, add_3_4bit_124_f, add_3_4bit_125_f, add_3_4bit_126_f,
       add_3_4bit_127_f, add_3_4bit_128_f, add_3_4bit_130_f, add_3_4bit_131_f, add_3_4bit_132_f,
       add_3_4bit_133_f, add_3_4bit_134_f, add_3_4bit_135_f, add_3_4bit_136_f, add_3_4bit_137_f,
       add_3_4bit_138_f, add_3_4bit_139_f, add_3_4bit_141_f, add_3_4bit_142_f, add_3_4bit_143_f,
       add_3_4bit_144_f, add_3_4bit_145_f, add_3_4bit_146_f, add_3_4bit_147_f, add_3_4bit_149_f,
       add_3_4bit_150_f, add_3_4bit_151_f, add_3_4bit_152_f, add_3_4bit_154_f;
  wire [3:3] add_3_4bit_1_f_2, add_3_4bit_2_f_2, add_3_4bit_3_f_2, add_3_4bit_4_f_2, add_3_4bit_5_f_2,
       add_3_4bit_6_f_2, add_3_4bit_7_f_2, add_3_4bit_8_f_2, add_3_4bit_9_f_2, add_3_4bit_10_f_2,
       add_3_4bit_11_f_2, add_3_4bit_12_f_2, add_3_4bit_13_f_2, add_3_4bit_14_f_2, add_3_4bit_15_f_2,
       add_3_4bit_16_f_2, add_3_4bit_17_f_2, add_3_4bit_18_f_2, add_3_4bit_19_f_2, add_3_4bit_20_f_2,
       add_3_4bit_21_f_2, add_3_4bit_22_f_2, add_3_4bit_23_f_2, add_3_4bit_24_f_2, add_3_4bit_25_f_2,
       add_3_4bit_26_f_2, add_3_4bit_27_f_2, add_3_4bit_28_f_2, add_3_4bit_56_f_2, add_3_4bit_57_f_2,
       add_3_4bit_58_f_2, add_3_4bit_59_f_2, add_3_4bit_60_f_2, add_3_4bit_61_f_2, add_3_4bit_62_f_2,
       add_3_4bit_63_f_2, add_3_4bit_64_f_2, add_3_4bit_65_f_2, add_3_4bit_66_f_2, add_3_4bit_67_f_2,
       add_3_4bit_68_f_2, add_3_4bit_69_f_2, add_3_4bit_70_f_2, add_3_4bit_71_f_2, add_3_4bit_72_f_2,
       add_3_4bit_73_f_2, add_3_4bit_74_f_2, add_3_4bit_75_f_2, add_3_4bit_76_f_2, add_3_4bit_77_f_2,
       add_3_4bit_79_f_2, add_3_4bit_80_f_2, add_3_4bit_81_f_2, add_3_4bit_82_f_2, add_3_4bit_83_f_2,
       add_3_4bit_84_f_2, add_3_4bit_85_f_2, add_3_4bit_86_f_2, add_3_4bit_87_f_2, add_3_4bit_88_f_2,
       add_3_4bit_89_f_2, add_3_4bit_90_f_2, add_3_4bit_91_f_2, add_3_4bit_92_f_2, add_3_4bit_93_f_2,
       add_3_4bit_94_f_2, add_3_4bit_95_f_2, add_3_4bit_96_f_2, add_3_4bit_97_f_2, add_3_4bit_99_f_2,
       add_3_4bit_100_f_2, add_3_4bit_101_f_2, add_3_4bit_102_f_2, add_3_4bit_103_f_2, add_3_4bit_104_f_2,
       add_3_4bit_105_f_2, add_3_4bit_106_f_2, add_3_4bit_107_f_2, add_3_4bit_108_f_2, add_3_4bit_109_f_2,
       add_3_4bit_110_f_2, add_3_4bit_111_f_2, add_3_4bit_112_f_2, add_3_4bit_113_f_2, add_3_4bit_114_f_2,
       add_3_4bit_116_f_2, add_3_4bit_117_f_2, add_3_4bit_118_f_2, add_3_4bit_119_f_2, add_3_4bit_120_f_2,
       add_3_4bit_121_f_2, add_3_4bit_122_f_2, add_3_4bit_123_f_2, add_3_4bit_124_f_2, add_3_4bit_125_f_2,
       add_3_4bit_126_f_2, add_3_4bit_127_f_2, add_3_4bit_128_f_2, add_3_4bit_130_f_2, add_3_4bit_131_f_2,
       add_3_4bit_132_f_2, add_3_4bit_133_f_2, add_3_4bit_134_f_2, add_3_4bit_135_f_2, add_3_4bit_136_f_2,
       add_3_4bit_137_f_2, add_3_4bit_138_f_2, add_3_4bit_139_f_2, add_3_4bit_141_f_2, add_3_4bit_142_f_2,
       add_3_4bit_143_f_2, add_3_4bit_144_f_2, add_3_4bit_145_f_2, add_3_4bit_146_f_2, add_3_4bit_147_f_2,
       add_3_4bit_149_f_2, add_3_4bit_150_f_2, add_3_4bit_151_f_2, add_3_4bit_152_f_2, add_3_4bit_154_f_2,
       add_3_4bit_155_f;

  Add_3_4bit add_3_4bit_1 (.A({1'b0, in_1[31:29]}), .F({add_3_4bit_1_f_2[3], add_3_4bit_1_f}));
  Add_3_4bit add_3_4bit_2 (.A({add_3_4bit_1_f, in_1[28]}), .F({add_3_4bit_2_f_2[3], add_3_4bit_2_f}));
  Add_3_4bit add_3_4bit_3 (.A({add_3_4bit_2_f, in_1[27]}), .F({add_3_4bit_3_f_2[3], add_3_4bit_3_f}));
  Add_3_4bit add_3_4bit_4 (.A({add_3_4bit_3_f, in_1[26]}), .F({add_3_4bit_4_f_2[3], add_3_4bit_4_f}));
  Add_3_4bit add_3_4bit_5 (.A({add_3_4bit_4_f, in_1[25]}), .F({add_3_4bit_5_f_2[3], add_3_4bit_5_f}));
  Add_3_4bit add_3_4bit_6 (.A({add_3_4bit_5_f, in_1[24]}), .F({add_3_4bit_6_f_2[3], add_3_4bit_6_f}));
  Add_3_4bit add_3_4bit_7 (.A({add_3_4bit_6_f, in_1[23]}), .F({add_3_4bit_7_f_2[3], add_3_4bit_7_f}));
  Add_3_4bit add_3_4bit_8 (.A({add_3_4bit_7_f, in_1[22]}), .F({add_3_4bit_8_f_2[3], add_3_4bit_8_f}));
  Add_3_4bit add_3_4bit_9 (.A({add_3_4bit_8_f, in_1[21]}), .F({add_3_4bit_9_f_2[3], add_3_4bit_9_f}));
  Add_3_4bit add_3_4bit_10 (.A({add_3_4bit_9_f, in_1[20]}), .F({add_3_4bit_10_f_2[3], add_3_4bit_10_f}));
  Add_3_4bit add_3_4bit_11 (.A({add_3_4bit_10_f, in_1[19]}), .F({add_3_4bit_11_f_2[3], add_3_4bit_11_f}));
  Add_3_4bit add_3_4bit_12 (.A({add_3_4bit_11_f, in_1[18]}), .F({add_3_4bit_12_f_2[3], add_3_4bit_12_f}));
  Add_3_4bit add_3_4bit_13 (.A({add_3_4bit_12_f, in_1[17]}), .F({add_3_4bit_13_f_2[3], add_3_4bit_13_f}));
  Add_3_4bit add_3_4bit_14 (.A({add_3_4bit_13_f, in_1[16]}), .F({add_3_4bit_14_f_2[3], add_3_4bit_14_f}));
  Add_3_4bit add_3_4bit_15 (.A({add_3_4bit_14_f, in_1[15]}), .F({add_3_4bit_15_f_2[3], add_3_4bit_15_f}));
  Add_3_4bit add_3_4bit_16 (.A({add_3_4bit_15_f, in_1[14]}), .F({add_3_4bit_16_f_2[3], add_3_4bit_16_f}));
  Add_3_4bit add_3_4bit_17 (.A({add_3_4bit_16_f, in_1[13]}), .F({add_3_4bit_17_f_2[3], add_3_4bit_17_f}));
  Add_3_4bit add_3_4bit_18 (.A({add_3_4bit_17_f, in_1[12]}), .F({add_3_4bit_18_f_2[3], add_3_4bit_18_f}));
  Add_3_4bit add_3_4bit_19 (.A({add_3_4bit_18_f, in_1[11]}), .F({add_3_4bit_19_f_2[3], add_3_4bit_19_f}));
  Add_3_4bit add_3_4bit_20 (.A({add_3_4bit_19_f, in_1[10]}), .F({add_3_4bit_20_f_2[3], add_3_4bit_20_f}));
  Add_3_4bit add_3_4bit_21 (.A({add_3_4bit_20_f, in_1[9]}), .F({add_3_4bit_21_f_2[3], add_3_4bit_21_f}));
  Add_3_4bit add_3_4bit_22 (.A({add_3_4bit_21_f, in_1[8]}), .F({add_3_4bit_22_f_2[3], add_3_4bit_22_f}));
  Add_3_4bit add_3_4bit_23 (.A({add_3_4bit_22_f, in_1[7]}), .F({add_3_4bit_23_f_2[3], add_3_4bit_23_f}));
  Add_3_4bit add_3_4bit_24 (.A({add_3_4bit_23_f, in_1[6]}), .F({add_3_4bit_24_f_2[3], add_3_4bit_24_f}));
  Add_3_4bit add_3_4bit_25 (.A({add_3_4bit_24_f, in_1[5]}), .F({add_3_4bit_25_f_2[3], add_3_4bit_25_f}));
  Add_3_4bit add_3_4bit_26 (.A({add_3_4bit_25_f, in_1[4]}), .F({add_3_4bit_26_f_2[3], add_3_4bit_26_f}));
  Add_3_4bit add_3_4bit_27 (.A({add_3_4bit_26_f, in_1[3]}), .F({add_3_4bit_27_f_2[3], add_3_4bit_27_f}));
  Add_3_4bit add_3_4bit_28 (.A({add_3_4bit_27_f, in_1[2]}), .F({add_3_4bit_28_f_2[3], add_3_4bit_28_f}));
  Add_3_4bit add_3_4bit_29 (.A({add_3_4bit_28_f, in_1[1]}), .F({T[0], O[3:1]}));
  Add_3_4bit add_3_4bit_30 (
    .A({1'b0, add_3_4bit_1_f_2[3], add_3_4bit_2_f_2[3], add_3_4bit_3_f_2[3]}), .F(add_3_4bit_30_f));
  Add_3_4bit add_3_4bit_31 (.A({add_3_4bit_30_f[2:0], add_3_4bit_4_f_2[3]}), .F(add_3_4bit_31_f));
  Add_3_4bit add_3_4bit_32 (.A({add_3_4bit_31_f[2:0], add_3_4bit_5_f_2[3]}), .F(add_3_4bit_32_f));
  Add_3_4bit add_3_4bit_33 (.A({add_3_4bit_32_f[2:0], add_3_4bit_6_f_2[3]}), .F(add_3_4bit_33_f));
  Add_3_4bit add_3_4bit_34 (.A({add_3_4bit_33_f[2:0], add_3_4bit_7_f_2[3]}), .F(add_3_4bit_34_f));
  Add_3_4bit add_3_4bit_35 (.A({add_3_4bit_34_f[2:0], add_3_4bit_8_f_2[3]}), .F(add_3_4bit_35_f));
  Add_3_4bit add_3_4bit_36 (.A({add_3_4bit_35_f[2:0], add_3_4bit_9_f_2[3]}), .F(add_3_4bit_36_f));
  Add_3_4bit add_3_4bit_37 (.A({add_3_4bit_36_f[2:0], add_3_4bit_10_f_2[3]}), .F(add_3_4bit_37_f));
  Add_3_4bit add_3_4bit_38 (.A({add_3_4bit_37_f[2:0], add_3_4bit_11_f_2[3]}), .F(add_3_4bit_38_f));
  Add_3_4bit add_3_4bit_39 (.A({add_3_4bit_38_f[2:0], add_3_4bit_12_f_2[3]}), .F(add_3_4bit_39_f));
  Add_3_4bit add_3_4bit_40 (.A({add_3_4bit_39_f[2:0], add_3_4bit_13_f_2[3]}), .F(add_3_4bit_40_f));
  Add_3_4bit add_3_4bit_41 (.A({add_3_4bit_40_f[2:0], add_3_4bit_14_f_2[3]}), .F(add_3_4bit_41_f));
  Add_3_4bit add_3_4bit_42 (.A({add_3_4bit_41_f[2:0], add_3_4bit_15_f_2[3]}), .F(add_3_4bit_42_f));
  Add_3_4bit add_3_4bit_43 (.A({add_3_4bit_42_f[2:0], add_3_4bit_16_f_2[3]}), .F(add_3_4bit_43_f));
  Add_3_4bit add_3_4bit_44 (.A({add_3_4bit_43_f[2:0], add_3_4bit_17_f_2[3]}), .F(add_3_4bit_44_f));
  Add_3_4bit add_3_4bit_45 (.A({add_3_4bit_44_f[2:0], add_3_4bit_18_f_2[3]}), .F(add_3_4bit_45_f));
  Add_3_4bit add_3_4bit_46 (.A({add_3_4bit_45_f[2:0], add_3_4bit_19_f_2[3]}), .F(add_3_4bit_46_f));
  Add_3_4bit add_3_4bit_47 (.A({add_3_4bit_46_f[2:0], add_3_4bit_20_f_2[3]}), .F(add_3_4bit_47_f));
  Add_3_4bit add_3_4bit_48 (.A({add_3_4bit_47_f[2:0], add_3_4bit_21_f_2[3]}), .F(add_3_4bit_48_f));
  Add_3_4bit add_3_4bit_49 (.A({add_3_4bit_48_f[2:0], add_3_4bit_22_f_2[3]}), .F(add_3_4bit_49_f));
  Add_3_4bit add_3_4bit_50 (.A({add_3_4bit_49_f[2:0], add_3_4bit_23_f_2[3]}), .F(add_3_4bit_50_f));
  Add_3_4bit add_3_4bit_51 (.A({add_3_4bit_50_f[2:0], add_3_4bit_24_f_2[3]}), .F(add_3_4bit_51_f));
  Add_3_4bit add_3_4bit_52 (.A({add_3_4bit_51_f[2:0], add_3_4bit_25_f_2[3]}), .F(add_3_4bit_52_f));
  Add_3_4bit add_3_4bit_53 (.A({add_3_4bit_52_f[2:0], add_3_4bit_26_f_2[3]}), .F(add_3_4bit_53_f));
  Add_3_4bit add_3_4bit_54 (.A({add_3_4bit_53_f[2:0], add_3_4bit_27_f_2[3]}), .F(add_3_4bit_54_f));
  Add_3_4bit add_3_4bit_55 (.A({add_3_4bit_54_f[2:0], add_3_4bit_28_f_2[3]}), .F({H[0], T[3:1]}));
  Add_3_4bit add_3_4bit_56 (
    .A({1'b0, add_3_4bit_30_f[3], add_3_4bit_31_f[3], add_3_4bit_32_f[3]}),
    .F({add_3_4bit_56_f_2[3], add_3_4bit_56_f}));
  Add_3_4bit add_3_4bit_57 (.A({add_3_4bit_56_f, add_3_4bit_33_f[3]}), .F({add_3_4bit_57_f_2[3], add_3_4bit_57_f}));
  Add_3_4bit add_3_4bit_58 (.A({add_3_4bit_57_f, add_3_4bit_34_f[3]}), .F({add_3_4bit_58_f_2[3], add_3_4bit_58_f}));
  Add_3_4bit add_3_4bit_59 (.A({add_3_4bit_58_f, add_3_4bit_35_f[3]}), .F({add_3_4bit_59_f_2[3], add_3_4bit_59_f}));
  Add_3_4bit add_3_4bit_60 (.A({add_3_4bit_59_f, add_3_4bit_36_f[3]}), .F({add_3_4bit_60_f_2[3], add_3_4bit_60_f}));
  Add_3_4bit add_3_4bit_61 (.A({add_3_4bit_60_f, add_3_4bit_37_f[3]}), .F({add_3_4bit_61_f_2[3], add_3_4bit_61_f}));
  Add_3_4bit add_3_4bit_62 (.A({add_3_4bit_61_f, add_3_4bit_38_f[3]}), .F({add_3_4bit_62_f_2[3], add_3_4bit_62_f}));
  Add_3_4bit add_3_4bit_63 (.A({add_3_4bit_62_f, add_3_4bit_39_f[3]}), .F({add_3_4bit_63_f_2[3], add_3_4bit_63_f}));
  Add_3_4bit add_3_4bit_64 (.A({add_3_4bit_63_f, add_3_4bit_40_f[3]}), .F({add_3_4bit_64_f_2[3], add_3_4bit_64_f}));
  Add_3_4bit add_3_4bit_65 (.A({add_3_4bit_64_f, add_3_4bit_41_f[3]}), .F({add_3_4bit_65_f_2[3], add_3_4bit_65_f}));
  Add_3_4bit add_3_4bit_66 (.A({add_3_4bit_65_f, add_3_4bit_42_f[3]}), .F({add_3_4bit_66_f_2[3], add_3_4bit_66_f}));
  Add_3_4bit add_3_4bit_67 (.A({add_3_4bit_66_f, add_3_4bit_43_f[3]}), .F({add_3_4bit_67_f_2[3], add_3_4bit_67_f}));
  Add_3_4bit add_3_4bit_68 (.A({add_3_4bit_67_f, add_3_4bit_44_f[3]}), .F({add_3_4bit_68_f_2[3], add_3_4bit_68_f}));
  Add_3_4bit add_3_4bit_69 (.A({add_3_4bit_68_f, add_3_4bit_45_f[3]}), .F({add_3_4bit_69_f_2[3], add_3_4bit_69_f}));
  Add_3_4bit add_3_4bit_70 (.A({add_3_4bit_69_f, add_3_4bit_46_f[3]}), .F({add_3_4bit_70_f_2[3], add_3_4bit_70_f}));
  Add_3_4bit add_3_4bit_71 (.A({add_3_4bit_70_f, add_3_4bit_47_f[3]}), .F({add_3_4bit_71_f_2[3], add_3_4bit_71_f}));
  Add_3_4bit add_3_4bit_72 (.A({add_3_4bit_71_f, add_3_4bit_48_f[3]}), .F({add_3_4bit_72_f_2[3], add_3_4bit_72_f}));
  Add_3_4bit add_3_4bit_73 (.A({add_3_4bit_72_f, add_3_4bit_49_f[3]}), .F({add_3_4bit_73_f_2[3], add_3_4bit_73_f}));
  Add_3_4bit add_3_4bit_74 (.A({add_3_4bit_73_f, add_3_4bit_50_f[3]}), .F({add_3_4bit_74_f_2[3], add_3_4bit_74_f}));
  Add_3_4bit add_3_4bit_75 (.A({add_3_4bit_74_f, add_3_4bit_51_f[3]}), .F({add_3_4bit_75_f_2[3], add_3_4bit_75_f}));
  Add_3_4bit add_3_4bit_76 (.A({add_3_4bit_75_f, add_3_4bit_52_f[3]}), .F({add_3_4bit_76_f_2[3], add_3_4bit_76_f}));
  Add_3_4bit add_3_4bit_77 (.A({add_3_4bit_76_f, add_3_4bit_53_f[3]}), .F({add_3_4bit_77_f_2[3], add_3_4bit_77_f}));
  Add_3_4bit add_3_4bit_78 (.A({add_3_4bit_77_f, add_3_4bit_54_f[3]}), .F({OT[0], H[3:1]}));
  Add_3_4bit add_3_4bit_79 (
    .A({1'b0, add_3_4bit_56_f_2[3], add_3_4bit_57_f_2[3], add_3_4bit_58_f_2[3]}),
    .F({add_3_4bit_79_f_2[3], add_3_4bit_79_f}));
  Add_3_4bit add_3_4bit_80 (.A({add_3_4bit_79_f, add_3_4bit_59_f_2[3]}), .F({add_3_4bit_80_f_2[3], add_3_4bit_80_f}));
  Add_3_4bit add_3_4bit_81 (.A({add_3_4bit_80_f, add_3_4bit_60_f_2[3]}), .F({add_3_4bit_81_f_2[3], add_3_4bit_81_f}));
  Add_3_4bit add_3_4bit_82 (.A({add_3_4bit_81_f, add_3_4bit_61_f_2[3]}), .F({add_3_4bit_82_f_2[3], add_3_4bit_82_f}));
  Add_3_4bit add_3_4bit_83 (.A({add_3_4bit_82_f, add_3_4bit_62_f_2[3]}), .F({add_3_4bit_83_f_2[3], add_3_4bit_83_f}));
  Add_3_4bit add_3_4bit_84 (.A({add_3_4bit_83_f, add_3_4bit_63_f_2[3]}), .F({add_3_4bit_84_f_2[3], add_3_4bit_84_f}));
  Add_3_4bit add_3_4bit_85 (.A({add_3_4bit_84_f, add_3_4bit_64_f_2[3]}), .F({add_3_4bit_85_f_2[3], add_3_4bit_85_f}));
  Add_3_4bit add_3_4bit_86 (.A({add_3_4bit_85_f, add_3_4bit_65_f_2[3]}), .F({add_3_4bit_86_f_2[3], add_3_4bit_86_f}));
  Add_3_4bit add_3_4bit_87 (.A({add_3_4bit_86_f, add_3_4bit_66_f_2[3]}), .F({add_3_4bit_87_f_2[3], add_3_4bit_87_f}));
  Add_3_4bit add_3_4bit_88 (.A({add_3_4bit_87_f, add_3_4bit_67_f_2[3]}), .F({add_3_4bit_88_f_2[3], add_3_4bit_88_f}));
  Add_3_4bit add_3_4bit_89 (.A({add_3_4bit_88_f, add_3_4bit_68_f_2[3]}), .F({add_3_4bit_89_f_2[3], add_3_4bit_89_f}));
  Add_3_4bit add_3_4bit_90 (.A({add_3_4bit_89_f, add_3_4bit_69_f_2[3]}), .F({add_3_4bit_90_f_2[3], add_3_4bit_90_f}));
  Add_3_4bit add_3_4bit_91 (.A({add_3_4bit_90_f, add_3_4bit_70_f_2[3]}), .F({add_3_4bit_91_f_2[3], add_3_4bit_91_f}));
  Add_3_4bit add_3_4bit_92 (.A({add_3_4bit_91_f, add_3_4bit_71_f_2[3]}), .F({add_3_4bit_92_f_2[3], add_3_4bit_92_f}));
  Add_3_4bit add_3_4bit_93 (.A({add_3_4bit_92_f, add_3_4bit_72_f_2[3]}), .F({add_3_4bit_93_f_2[3], add_3_4bit_93_f}));
  Add_3_4bit add_3_4bit_94 (.A({add_3_4bit_93_f, add_3_4bit_73_f_2[3]}), .F({add_3_4bit_94_f_2[3], add_3_4bit_94_f}));
  Add_3_4bit add_3_4bit_95 (.A({add_3_4bit_94_f, add_3_4bit_74_f_2[3]}), .F({add_3_4bit_95_f_2[3], add_3_4bit_95_f}));
  Add_3_4bit add_3_4bit_96 (.A({add_3_4bit_95_f, add_3_4bit_75_f_2[3]}), .F({add_3_4bit_96_f_2[3], add_3_4bit_96_f}));
  Add_3_4bit add_3_4bit_97 (.A({add_3_4bit_96_f, add_3_4bit_76_f_2[3]}), .F({add_3_4bit_97_f_2[3], add_3_4bit_97_f}));
  Add_3_4bit add_3_4bit_98 (.A({add_3_4bit_97_f, add_3_4bit_77_f_2[3]}), .F({TT[0], OT[3:1]}));
  Add_3_4bit add_3_4bit_99 (
    .A({1'b0, add_3_4bit_79_f_2[3], add_3_4bit_80_f_2[3], add_3_4bit_81_f_2[3]}),
    .F({add_3_4bit_99_f_2[3], add_3_4bit_99_f}));
  Add_3_4bit add_3_4bit_100 (
    .A({add_3_4bit_99_f, add_3_4bit_82_f_2[3]}), .F({add_3_4bit_100_f_2[3], add_3_4bit_100_f}));
  Add_3_4bit add_3_4bit_101 (
    .A({add_3_4bit_100_f, add_3_4bit_83_f_2[3]}), .F({add_3_4bit_101_f_2[3], add_3_4bit_101_f}));
  Add_3_4bit add_3_4bit_102 (
    .A({add_3_4bit_101_f, add_3_4bit_84_f_2[3]}), .F({add_3_4bit_102_f_2[3], add_3_4bit_102_f}));
  Add_3_4bit add_3_4bit_103 (
    .A({add_3_4bit_102_f, add_3_4bit_85_f_2[3]}), .F({add_3_4bit_103_f_2[3], add_3_4bit_103_f}));
  Add_3_4bit add_3_4bit_104 (
    .A({add_3_4bit_103_f, add_3_4bit_86_f_2[3]}), .F({add_3_4bit_104_f_2[3], add_3_4bit_104_f}));
  Add_3_4bit add_3_4bit_105 (
    .A({add_3_4bit_104_f, add_3_4bit_87_f_2[3]}), .F({add_3_4bit_105_f_2[3], add_3_4bit_105_f}));
  Add_3_4bit add_3_4bit_106 (
    .A({add_3_4bit_105_f, add_3_4bit_88_f_2[3]}), .F({add_3_4bit_106_f_2[3], add_3_4bit_106_f}));
  Add_3_4bit add_3_4bit_107 (
    .A({add_3_4bit_106_f, add_3_4bit_89_f_2[3]}), .F({add_3_4bit_107_f_2[3], add_3_4bit_107_f}));
  Add_3_4bit add_3_4bit_108 (
    .A({add_3_4bit_107_f, add_3_4bit_90_f_2[3]}), .F({add_3_4bit_108_f_2[3], add_3_4bit_108_f}));
  Add_3_4bit add_3_4bit_109 (
    .A({add_3_4bit_108_f, add_3_4bit_91_f_2[3]}), .F({add_3_4bit_109_f_2[3], add_3_4bit_109_f}));
  Add_3_4bit add_3_4bit_110 (
    .A({add_3_4bit_109_f, add_3_4bit_92_f_2[3]}), .F({add_3_4bit_110_f_2[3], add_3_4bit_110_f}));
  Add_3_4bit add_3_4bit_111 (
    .A({add_3_4bit_110_f, add_3_4bit_93_f_2[3]}), .F({add_3_4bit_111_f_2[3], add_3_4bit_111_f}));
  Add_3_4bit add_3_4bit_112 (
    .A({add_3_4bit_111_f, add_3_4bit_94_f_2[3]}), .F({add_3_4bit_112_f_2[3], add_3_4bit_112_f}));
  Add_3_4bit add_3_4bit_113 (
    .A({add_3_4bit_112_f, add_3_4bit_95_f_2[3]}), .F({add_3_4bit_113_f_2[3], add_3_4bit_113_f}));
  Add_3_4bit add_3_4bit_114 (
    .A({add_3_4bit_113_f, add_3_4bit_96_f_2[3]}), .F({add_3_4bit_114_f_2[3], add_3_4bit_114_f}));
  Add_3_4bit add_3_4bit_115 (.A({add_3_4bit_114_f, add_3_4bit_97_f_2[3]}), .F({HT[0], TT[3:1]}));
  Add_3_4bit add_3_4bit_116 (
    .A({1'b0, add_3_4bit_99_f_2[3], add_3_4bit_100_f_2[3], add_3_4bit_101_f_2[3]}),
    .F({add_3_4bit_116_f_2[3], add_3_4bit_116_f}));
  Add_3_4bit add_3_4bit_117 (
    .A({add_3_4bit_116_f, add_3_4bit_102_f_2[3]}), .F({add_3_4bit_117_f_2[3], add_3_4bit_117_f}));
  Add_3_4bit add_3_4bit_118 (
    .A({add_3_4bit_117_f, add_3_4bit_103_f_2[3]}), .F({add_3_4bit_118_f_2[3], add_3_4bit_118_f}));
  Add_3_4bit add_3_4bit_119 (
    .A({add_3_4bit_118_f, add_3_4bit_104_f_2[3]}), .F({add_3_4bit_119_f_2[3], add_3_4bit_119_f}));
  Add_3_4bit add_3_4bit_120 (
    .A({add_3_4bit_119_f, add_3_4bit_105_f_2[3]}), .F({add_3_4bit_120_f_2[3], add_3_4bit_120_f}));
  Add_3_4bit add_3_4bit_121 (
    .A({add_3_4bit_120_f, add_3_4bit_106_f_2[3]}), .F({add_3_4bit_121_f_2[3], add_3_4bit_121_f}));
  Add_3_4bit add_3_4bit_122 (
    .A({add_3_4bit_121_f, add_3_4bit_107_f_2[3]}), .F({add_3_4bit_122_f_2[3], add_3_4bit_122_f}));
  Add_3_4bit add_3_4bit_123 (
    .A({add_3_4bit_122_f, add_3_4bit_108_f_2[3]}), .F({add_3_4bit_123_f_2[3], add_3_4bit_123_f}));
  Add_3_4bit add_3_4bit_124 (
    .A({add_3_4bit_123_f, add_3_4bit_109_f_2[3]}), .F({add_3_4bit_124_f_2[3], add_3_4bit_124_f}));
  Add_3_4bit add_3_4bit_125 (
    .A({add_3_4bit_124_f, add_3_4bit_110_f_2[3]}), .F({add_3_4bit_125_f_2[3], add_3_4bit_125_f}));
  Add_3_4bit add_3_4bit_126 (
    .A({add_3_4bit_125_f, add_3_4bit_111_f_2[3]}), .F({add_3_4bit_126_f_2[3], add_3_4bit_126_f}));
  Add_3_4bit add_3_4bit_127 (
    .A({add_3_4bit_126_f, add_3_4bit_112_f_2[3]}), .F({add_3_4bit_127_f_2[3], add_3_4bit_127_f}));
  Add_3_4bit add_3_4bit_128 (
    .A({add_3_4bit_127_f, add_3_4bit_113_f_2[3]}), .F({add_3_4bit_128_f_2[3], add_3_4bit_128_f}));
  Add_3_4bit add_3_4bit_129 (.A({add_3_4bit_128_f, add_3_4bit_114_f_2[3]}), .F({OM[0], HT[3:1]}));
  Add_3_4bit add_3_4bit_130 (
    .A({1'b0, add_3_4bit_116_f_2[3], add_3_4bit_117_f_2[3], add_3_4bit_118_f_2[3]}),
    .F({add_3_4bit_130_f_2[3], add_3_4bit_130_f}));
  Add_3_4bit add_3_4bit_131 (
    .A({add_3_4bit_130_f, add_3_4bit_119_f_2[3]}), .F({add_3_4bit_131_f_2[3], add_3_4bit_131_f}));
  Add_3_4bit add_3_4bit_132 (
    .A({add_3_4bit_131_f, add_3_4bit_120_f_2[3]}), .F({add_3_4bit_132_f_2[3], add_3_4bit_132_f}));
  Add_3_4bit add_3_4bit_133 (
    .A({add_3_4bit_132_f, add_3_4bit_121_f_2[3]}), .F({add_3_4bit_133_f_2[3], add_3_4bit_133_f}));
  Add_3_4bit add_3_4bit_134 (
    .A({add_3_4bit_133_f, add_3_4bit_122_f_2[3]}), .F({add_3_4bit_134_f_2[3], add_3_4bit_134_f}));
  Add_3_4bit add_3_4bit_135 (
    .A({add_3_4bit_134_f, add_3_4bit_123_f_2[3]}), .F({add_3_4bit_135_f_2[3], add_3_4bit_135_f}));
  Add_3_4bit add_3_4bit_136 (
    .A({add_3_4bit_135_f, add_3_4bit_124_f_2[3]}), .F({add_3_4bit_136_f_2[3], add_3_4bit_136_f}));
  Add_3_4bit add_3_4bit_137 (
    .A({add_3_4bit_136_f, add_3_4bit_125_f_2[3]}), .F({add_3_4bit_137_f_2[3], add_3_4bit_137_f}));
  Add_3_4bit add_3_4bit_138 (
    .A({add_3_4bit_137_f, add_3_4bit_126_f_2[3]}), .F({add_3_4bit_138_f_2[3], add_3_4bit_138_f}));
  Add_3_4bit add_3_4bit_139 (
    .A({add_3_4bit_138_f, add_3_4bit_127_f_2[3]}), .F({add_3_4bit_139_f_2[3], add_3_4bit_139_f}));
  Add_3_4bit add_3_4bit_140 (.A({add_3_4bit_139_f, add_3_4bit_128_f_2[3]}), .F({TM[0], OM[3:1]}));
  Add_3_4bit add_3_4bit_141 (
    .A({1'b0, add_3_4bit_130_f_2[3], add_3_4bit_131_f_2[3], add_3_4bit_132_f_2[3]}),
    .F({add_3_4bit_141_f_2[3], add_3_4bit_141_f}));
  Add_3_4bit add_3_4bit_142 (
    .A({add_3_4bit_141_f, add_3_4bit_133_f_2[3]}), .F({add_3_4bit_142_f_2[3], add_3_4bit_142_f}));
  Add_3_4bit add_3_4bit_143 (
    .A({add_3_4bit_142_f, add_3_4bit_134_f_2[3]}), .F({add_3_4bit_143_f_2[3], add_3_4bit_143_f}));
  Add_3_4bit add_3_4bit_144 (
    .A({add_3_4bit_143_f, add_3_4bit_135_f_2[3]}), .F({add_3_4bit_144_f_2[3], add_3_4bit_144_f}));
  Add_3_4bit add_3_4bit_145 (
    .A({add_3_4bit_144_f, add_3_4bit_136_f_2[3]}), .F({add_3_4bit_145_f_2[3], add_3_4bit_145_f}));
  Add_3_4bit add_3_4bit_146 (
    .A({add_3_4bit_145_f, add_3_4bit_137_f_2[3]}), .F({add_3_4bit_146_f_2[3], add_3_4bit_146_f}));
  Add_3_4bit add_3_4bit_147 (
    .A({add_3_4bit_146_f, add_3_4bit_138_f_2[3]}), .F({add_3_4bit_147_f_2[3], add_3_4bit_147_f}));
  Add_3_4bit add_3_4bit_148 (.A({add_3_4bit_147_f, add_3_4bit_139_f_2[3]}), .F({HM[0], TM[3:1]}));
  Add_3_4bit add_3_4bit_149 (
    .A({1'b0, add_3_4bit_141_f_2[3], add_3_4bit_142_f_2[3], add_3_4bit_143_f_2[3]}),
    .F({add_3_4bit_149_f_2[3], add_3_4bit_149_f}));
  Add_3_4bit add_3_4bit_150 (
    .A({add_3_4bit_149_f, add_3_4bit_144_f_2[3]}), .F({add_3_4bit_150_f_2[3], add_3_4bit_150_f}));
  Add_3_4bit add_3_4bit_151 (
    .A({add_3_4bit_150_f, add_3_4bit_145_f_2[3]}), .F({add_3_4bit_151_f_2[3], add_3_4bit_151_f}));
  Add_3_4bit add_3_4bit_152 (
    .A({add_3_4bit_151_f, add_3_4bit_146_f_2[3]}), .F({add_3_4bit_152_f_2[3], add_3_4bit_152_f}));
  Add_3_4bit add_3_4bit_153 (.A({add_3_4bit_152_f, add_3_4bit_147_f_2[3]}), .F({OB[0], HM[3:1]}));
  Add_3_4bit add_3_4bit_154 (
    .A({1'b0, add_3_4bit_149_f_2[3], add_3_4bit_150_f_2[3], add_3_4bit_151_f_2[3]}),
    .F({add_3_4bit_154_f_2[3], add_3_4bit_154_f}));
  Add_3_4bit add_3_4bit_155 (.A({add_3_4bit_154_f, add_3_4bit_152_f_2[3]}), .F({add_3_4bit_155_f[3], OB[3:1]}));

  assign O[0] = in_1[0];
endmodule

module BCD_TO_DISPLAY_32bit (
  input  [31:0] Din,
  input  Enable,
  input  CLK,
  output [6:0] Dout,
  output DE,
  output Reset
);

  wire d_ff_1_q, d_ff_2_q, nor_1_out, not_1_out, or_1_out, or_2_out, or_3_out, or_4_out, or_5_out, or_6_out,
       or_7_out, or_8_out, or_9_out, or_10_out, RI;
  wire [3:0] Count, counter_1_q, double_dabble_32bit_1_h, double_dabble_32bit_1_hm, double_dabble_32bit_1_ht,
       double_dabble_32bit_1_o, double_dabble_32bit_1_ob, double_dabble_32bit_1_om, double_dabble_32bit_1_ot,
       double_dabble_32bit_1_t, double_dabble_32bit_1_tm, double_dabble_32bit_1_tt, invert_4bit_1_invert4,
       multiplexer_1_out, priority_encoder_1_out;
  wire [7:7] add_8bit_1_add8;

  or or_1 (or_1_out, double_dabble_32bit_1_ob[0], double_dabble_32bit_1_ob[1], double_dabble_32bit_1_ob[2], double_dabble_32bit_1_ob[3]);
  D_Flip_Flop d_ff_1 (.D(Enable), .clk(CLK), .Q(d_ff_1_q), .reset(d_ff_2_q));  // open: Qn, preset
  nor nor_1 (nor_1_out, CLK, DE);
  D_Flip_Flop d_ff_2 (.D(RI), .clk(CLK), .Q(d_ff_2_q));  // open: Qn, preset, reset
  or or_2 (or_2_out, double_dabble_32bit_1_hm[0], double_dabble_32bit_1_hm[1], double_dabble_32bit_1_hm[2], double_dabble_32bit_1_hm[3]);
  D_Flip_Flop d_ff_3 (.D(d_ff_1_q), .clk(nor_1_out), .Q(DE), .reset(d_ff_2_q));  // open: Qn, preset
  or or_3 (or_3_out, double_dabble_32bit_1_tm[0], double_dabble_32bit_1_tm[1], double_dabble_32bit_1_tm[2], double_dabble_32bit_1_tm[3]);
  or or_4 (or_4_out, double_dabble_32bit_1_om[0], double_dabble_32bit_1_om[1], double_dabble_32bit_1_om[2], double_dabble_32bit_1_om[3]);
  // Probe on Din
  or or_5 (or_5_out, double_dabble_32bit_1_ht[0], double_dabble_32bit_1_ht[1], double_dabble_32bit_1_ht[2], double_dabble_32bit_1_ht[3]);
  and and_1 (RI, counter_1_q[0], counter_1_q[3]);
  or or_6 (or_6_out, double_dabble_32bit_1_tt[0], double_dabble_32bit_1_tt[1], double_dabble_32bit_1_tt[2], double_dabble_32bit_1_tt[3]);
  not not_1 (not_1_out, DE);
  Double_Dabble_32bit double_dabble_32bit_1 (
    .in_1(Din), .OB(double_dabble_32bit_1_ob), .HM(double_dabble_32bit_1_hm), .TM(double_dabble_32bit_1_tm),
    .OM(double_dabble_32bit_1_om), .HT(double_dabble_32bit_1_ht), .TT(double_dabble_32bit_1_tt),
    .OT(double_dabble_32bit_1_ot), .H(double_dabble_32bit_1_h), .T(double_dabble_32bit_1_t),
    .O(double_dabble_32bit_1_o));
  Counter #(.max('hf), .width(4)) counter_1 (
    .load(not_1_out), .D(Count), .count(DE), .Q(counter_1_q), .clk(CLK));  // open: carry, up, clr
  or or_7 (or_7_out, double_dabble_32bit_1_ot[0], double_dabble_32bit_1_ot[1], double_dabble_32bit_1_ot[2], double_dabble_32bit_1_ot[3]);
  or or_8 (or_8_out, double_dabble_32bit_1_h[0], double_dabble_32bit_1_h[1], double_dabble_32bit_1_h[2], double_dabble_32bit_1_h[3]);
  or or_9 (or_9_out, double_dabble_32bit_1_t[0], double_dabble_32bit_1_t[1], double_dabble_32bit_1_t[2], double_dabble_32bit_1_t[3]);
  Multiplexer #(.select(4), .width(4)) multiplexer_1 (
    .in0(double_dabble_32bit_1_ob), .in1(double_dabble_32bit_1_hm), .in2(double_dabble_32bit_1_tm),
    .in3(double_dabble_32bit_1_om), .in4(double_dabble_32bit_1_ht), .in5(double_dabble_32bit_1_tt),
    .in6(double_dabble_32bit_1_ot), .in7(double_dabble_32bit_1_h), .in8(double_dabble_32bit_1_t),
    .in9(double_dabble_32bit_1_o), .in10(4'b0000), .in11(4'b0000), .in12(4'b0000), .in13(4'b0000),
    .in14(4'b0000), .in15(4'b0000), .out(multiplexer_1_out), .sel(counter_1_q));
  or or_10 (or_10_out, double_dabble_32bit_1_o[0], double_dabble_32bit_1_o[1], double_dabble_32bit_1_o[2], double_dabble_32bit_1_o[3]);
  // Probe on multiplexer_1_out
  Priority_Encoder #(.select(4)) priority_encoder_1 (
    .in0(or_10_out), .in1(or_9_out), .in2(or_8_out), .in3(or_7_out), .in4(or_6_out), .in5(or_5_out),
    .in6(or_4_out), .in7(or_3_out), .in8(or_2_out), .in9(or_1_out), .in10(1'b0), .in11(1'b0), .in12(1'b0),
    .in13(1'b0), .in14(1'b0), .in15(1'b0), .out(priority_encoder_1_out));  // open: gs, en_out, en_in
  ADD_8bit add_8bit_1 (
    .A({4'b0000, multiplexer_1_out}), .B(8'h30), .ADD8({add_8bit_1_add8[7], Dout}));  // open: Cin, Cout
  Invert_4bit invert_4bit_1 (.A(priority_encoder_1_out), .Invert4(invert_4bit_1_invert4));
  and and_2 (Reset, DE, RI);
  Add_4bit add_4bit_1 (.A(4'b1001), .B(invert_4bit_1_invert4), .Cin(1'b1), .ADD4(Count));  // open: Cout
  // Probe on Count

  // Other names for the same wires on the sheet: Data[31:0] = Din; E = DE
endmodule

module register_4bit (
  input  [3:0] Din,
  input  Write,
  input  Clk,
  output [3:0] Dout
);

  wire multiplexer_1_out, multiplexer_2_out, multiplexer_3_out, multiplexer_4_out;

  D_Flip_Flop d_ff_1 (.D(multiplexer_1_out), .clk(Clk), .Q(Dout[0]));  // open: Qn, preset, reset
  Multiplexer multiplexer_1 (.in0(Dout[0]), .in1(Din[0]), .out(multiplexer_1_out), .sel(Write));
  D_Flip_Flop d_ff_2 (.D(multiplexer_2_out), .clk(Clk), .Q(Dout[1]));  // open: Qn, preset, reset
  Multiplexer multiplexer_2 (.in0(Dout[1]), .in1(Din[1]), .out(multiplexer_2_out), .sel(Write));
  D_Flip_Flop d_ff_3 (.D(multiplexer_3_out), .clk(Clk), .Q(Dout[2]));  // open: Qn, preset, reset
  Multiplexer multiplexer_3 (.in0(Dout[2]), .in1(Din[2]), .out(multiplexer_3_out), .sel(Write));
  D_Flip_Flop d_ff_4 (.D(multiplexer_4_out), .clk(Clk), .Q(Dout[3]));  // open: Qn, preset, reset
  Multiplexer multiplexer_4 (.in0(Dout[3]), .in1(Din[3]), .out(multiplexer_4_out), .sel(Write));
endmodule

module Program_counter (
  input  [31:0] Data,
  input  Load,
  input  Enable,
  input  Clk,
  input  Reset,
  output [31:0] Count
);

  wire [31:0] add_32bit_1_add32, multiplexer_1_out;

  Multiplexer #(.width(32)) multiplexer_1 (.in0(add_32bit_1_add32), .in1(Data), .out(multiplexer_1_out), .sel(Load));
  Pull_Resistor #(.pull(1)) pull_resistor_1 (.node(Enable));
  Register_32bit register_32bit_1 (.Din(multiplexer_1_out), .Write(Enable), .Clk(Clk), .Reset(Reset), .Dout(Count));
  ADD_32bit add_32bit_1 (.A(Count), .Cin(1'b1), .ADD32(add_32bit_1_add32));  // open: B, Sub, Cout
endmodule
